// Logisim project LogsimG0603.circ as structural Verilog: 1 circuit, main circuit main
module main (
  input  x,
  input  y,
  input  w,
  input  z,
  input  x_2,
  input  y_2,
  input  w_2,
  input  z_2,
  input  x_3,
  input  y_3,
  input  w_3,
  input  z_3,
  input  x_4,
  input  y_4,
  input  w_4,
  input  z_4,
  input  x_5,
  input  y_5,
  input  w_5,
  input  z_5,
  output out_21,
  output out_22,
  output out_23,
  output out_24,
  output out_25
);

  wire and_1_out, and_2_out, and_3_out, and_4_out, and_5_out, and_6_out, and_7_out, and_8_out, and_9_out,
       and_10_out, and_11_out, and_12_out, not_1_out, not_2_out, not_3_out, not_4_out, not_5_out, not_6_out,
       not_7_out, not_8_out, not_9_out, not_10_out, not_11_out, not_12_out, not_13_out, not_14_out,
       not_15_out, not_16_out, not_17_out, not_18_out, not_19_out, not_20_out, not_21_out, not_22_out,
       not_23_out, not_24_out, or_1_out, or_2_out, or_3_out, or_4_out, or_5_out, or_6_out, or_7_out;

  not not_1 (not_1_out, z);
  not not_2 (not_2_out, w);
  not not_3 (not_3_out, w);
  not not_4 (not_4_out, y);
  not not_5 (not_5_out, x);
  not not_6 (not_6_out, z);
  or or_1 (or_1_out, y, not_7_out);
  not not_7 (not_7_out, x);
  not not_8 (not_8_out, y_2);
  not not_9 (not_9_out, x_2);
  or or_2 (or_2_out, w_2, not_10_out);
  not not_10 (not_10_out, w_2);
  not not_11 (not_11_out, w_2);
  not not_12 (not_12_out, w_2);
  not not_13 (not_13_out, z_3);
  not not_14 (not_14_out, w_3);
  or or_3 (or_3_out, z_4, not_15_out);
  not not_15 (not_15_out, x_4);
  not not_16 (not_16_out, w_5);
  and and_1 (and_1_out, not_1_out, not_2_out, x);
  and and_2 (and_2_out, z, not_3_out, not_4_out, not_5_out);
  and and_3 (and_3_out, not_6_out, w, or_1_out);
  and and_4 (and_4_out, w_2, w_2, y_2);
  and and_5 (and_5_out, not_8_out, not_9_out, or_2_out);
  and and_6 (and_6_out, not_11_out, not_12_out, x_2);
  and and_7 (and_7_out, z_3, w_3, y_3, not_17_out);
  not not_17 (not_17_out, x_3);
  not not_18 (not_18_out, y_3);
  and and_8 (and_8_out, not_18_out, not_19_out, or_4_out);
  not not_19 (not_19_out, x_3);
  or or_4 (or_4_out, not_13_out, not_14_out);
  and and_9 (and_9_out, w_3, x_3);
  not not_20 (not_20_out, z_4);
  and and_10 (and_10_out, not_20_out, w_4);
  not not_21 (not_21_out, w_4);
  and and_11 (and_11_out, not_21_out, y_4, or_3_out);
  or or_5 (or_5_out, z_5, not_22_out);
  not not_22 (not_22_out, w_5);
  and and_12 (and_12_out, z_5, not_16_out);
  or or_6 (or_6_out, and_12_out, not_23_out);
  not not_23 (not_23_out, y_5);
  or or_7 (or_7_out, x_5, not_24_out);
  not not_24 (not_24_out, x_5);
  or or_8 (out_21, and_1_out, and_2_out, and_3_out);
  or or_9 (out_22, and_4_out, and_5_out, and_6_out);
  or or_10 (out_24, and_10_out, and_11_out);
  and and_13 (out_25, or_5_out, or_6_out, or_7_out);
  or or_11 (out_23, and_7_out, and_8_out, and_9_out);

  assign z_2 = w_2;

  // Notes on the sheet:
  //   Letra a)
  //   Letra b)
  //   Letra c)
  //   Letra d)
  //   Letra e)
endmodule
