// Logisim project logsimG0605.circ as structural Verilog: 1 circuit, main circuit main
module main (
  input  x,
  input  y,
  input  z,
  input  x_2,
  input  y_2,
  input  z_2,
  output \saída ,
  output \saída_2 
);

  wire and_1_out, and_2_out, and_3_out, not_1_out, not_2_out, not_3_out, not_4_out, not_5_out, not_6_out,
       not_7_out, not_8_out, or_1_out, or_2_out, or_3_out;

  not not_1 (not_1_out, y);
  not not_2 (not_2_out, x);
  and and_1 (and_1_out, z, y);
  not not_3 (not_3_out, x);
  not not_4 (not_4_out, z_2);
  not not_5 (not_5_out, y_2);
  or or_1 (or_1_out, not_1_out, not_2_out);
  and and_2 (and_2_out, y, x);
  or or_2 (or_2_out, and_1_out, not_3_out);
  or or_3 (or_3_out, not_4_out, not_5_out);
  not not_6 (not_6_out, or_1_out);
  and and_3 (and_3_out, not_6_out, not_7_out);
  not not_7 (not_7_out, and_2_out);
  not not_8 (not_8_out, or_2_out);
  and and_4 (\saída_2 , or_3_out, x_2);
  or or_4 (\saída , and_3_out, not_8_out);

  // Notes on the sheet:
  //   Questão 5)
  //   Simplificação: x . ( y' + z' )
  //   Expressão original: [( y' + x' )' . ( x . y )'] + [( y . z ) + x' ]'
endmodule
