// Logisim project G1201.circ as structural Verilog: 1 circuit, main circuit main
module main (
  input  in_1
);

  wire clear_out, clock_1_out, j_k_ff_1_q, j_k_ff_2_q, j_k_ff_3_q, not_1_out, not_2_out, not_3_out, not_4_out;

  Clock clock_1 (.out(clock_1_out));
  not not_1 (not_1_out, in_1);
  Button clear (.out(clear_out));
  J_K_Flip_Flop j_k_ff_1 (
    .J(in_1), .clk(clock_1_out), .K(not_1_out), .Q(j_k_ff_1_q), .reset(clear_out));  // open: Qn, preset
  J_K_Flip_Flop j_k_ff_2 (
    .J(j_k_ff_1_q), .clk(clock_1_out), .K(not_2_out), .Q(j_k_ff_2_q), .reset(clear_out));  // open: Qn, preset
  not not_2 (not_2_out, j_k_ff_1_q);
  not not_3 (not_3_out, j_k_ff_2_q);
  J_K_Flip_Flop j_k_ff_3 (
    .J(j_k_ff_2_q), .clk(clock_1_out), .K(not_3_out), .Q(j_k_ff_3_q), .reset(clear_out));  // open: Qn, preset
  not not_4 (not_4_out, j_k_ff_3_q);
  J_K_Flip_Flop j_k_ff_4 (.J(j_k_ff_3_q), .clk(clock_1_out), .K(not_4_out), .reset(clear_out));  // open: Q, Qn, preset
endmodule
