// Logisim project G1202.circ as structural Verilog: 1 circuit, main circuit main
module main (
  input  entrada
);

  wire clear_out, clock_1_out, j_k_ff_1_q, j_k_ff_2_q, j_k_ff_3_q, j_k_ff_4_q, j_k_ff_5_q, j_k_ff_6_q,
       not_1_out, not_2_out, not_3_out, not_4_out, not_5_out, not_6_out, not_7_out, not_8_out;

  Button clear (.out(clear_out));
  Clock clock_1 (.out(clock_1_out));
  not not_1 (not_1_out, entrada);
  not not_2 (not_2_out, entrada);
  J_K_Flip_Flop j_k_ff_1 (
    .J(entrada), .clk(clock_1_out), .K(not_1_out), .Q(j_k_ff_1_q), .reset(clear_out));  // open: Qn, preset
  J_K_Flip_Flop j_k_ff_2 (
    .J(entrada), .clk(clock_1_out), .K(not_2_out), .Q(j_k_ff_2_q), .reset(clear_out));  // open: Qn, preset
  J_K_Flip_Flop j_k_ff_3 (
    .J(j_k_ff_1_q), .clk(clock_1_out), .K(not_3_out), .Q(j_k_ff_3_q), .reset(clear_out));  // open: Qn, preset
  not not_3 (not_3_out, j_k_ff_1_q);
  J_K_Flip_Flop j_k_ff_4 (
    .J(j_k_ff_2_q), .clk(clock_1_out), .K(not_4_out), .Q(j_k_ff_4_q), .reset(clear_out));  // open: Qn, preset
  not not_4 (not_4_out, j_k_ff_2_q);
  not not_5 (not_5_out, j_k_ff_3_q);
  not not_6 (not_6_out, j_k_ff_4_q);
  J_K_Flip_Flop j_k_ff_5 (
    .J(j_k_ff_3_q), .clk(clock_1_out), .K(not_5_out), .Q(j_k_ff_5_q), .reset(clear_out));  // open: Qn, preset
  not not_7 (not_7_out, j_k_ff_5_q);
  J_K_Flip_Flop j_k_ff_6 (
    .J(j_k_ff_4_q), .clk(clock_1_out), .K(not_6_out), .Q(j_k_ff_6_q), .reset(clear_out));  // open: Qn, preset
  not not_8 (not_8_out, j_k_ff_6_q);
  J_K_Flip_Flop j_k_ff_7 (.J(j_k_ff_5_q), .clk(clock_1_out), .K(not_7_out), .reset(clear_out));  // open: Q, Qn, preset
  J_K_Flip_Flop j_k_ff_8 (.J(j_k_ff_6_q), .clk(clock_1_out), .K(not_8_out), .reset(clear_out));  // open: Q, Qn, preset
endmodule
