// Logisim project G1207.circ as structural Verilog: 1 circuit, main circuit main
module main (
  input  entrada_1,
  input  entrada_2,
  input  entrada_3,
  input  entrada_4,
  input  entrada_5,
  input  entrada_6,
  input  entrada_7,
  input  entrada_8
);

  wire clear_1_out, clear_2_out, clear_3_out, clear_4_out, clear_5_out, clear_6_out, clear_7_out,
       clear_8_out, clock__global_out, j_k_ff_1_q, j_k_ff_2_q, j_k_ff_3_q, j_k_ff_4_q, j_k_ff_5_q,
       j_k_ff_6_q, j_k_ff_7_q, j_k_ff_8_q, j_k_ff_9_q, j_k_ff_10_q, j_k_ff_11_q, j_k_ff_12_q, j_k_ff_13_q,
       j_k_ff_14_q, j_k_ff_15_q, j_k_ff_16_q, j_k_ff_17_q, j_k_ff_18_q, j_k_ff_19_q, j_k_ff_20_q,
       j_k_ff_21_q, j_k_ff_22_q, j_k_ff_23_q, j_k_ff_24_q, j_k_ff_25_q, j_k_ff_26_q, j_k_ff_27_q,
       j_k_ff_28_q, j_k_ff_29_q, j_k_ff_30_q, j_k_ff_31_q, j_k_ff_32_q, j_k_ff_33_q, j_k_ff_34_q,
       j_k_ff_35_q, j_k_ff_36_q, j_k_ff_37_q, j_k_ff_38_q, j_k_ff_39_q, j_k_ff_40_q, j_k_ff_41_q,
       j_k_ff_42_q, j_k_ff_43_q, j_k_ff_44_q, j_k_ff_45_q, j_k_ff_46_q, j_k_ff_47_q, j_k_ff_48_q,
       j_k_ff_49_q, j_k_ff_50_q, j_k_ff_51_q, j_k_ff_52_q, j_k_ff_53_q, j_k_ff_54_q, j_k_ff_55_q,
       j_k_ff_56_q, j_k_ff_57_q, j_k_ff_58_q, j_k_ff_59_q, j_k_ff_60_q, j_k_ff_61_q, j_k_ff_62_q,
       j_k_ff_63_q, j_k_ff_64_q, j_k_ff_65_q, j_k_ff_66_q, j_k_ff_67_q, j_k_ff_68_q, j_k_ff_69_q,
       j_k_ff_70_q, j_k_ff_71_q, j_k_ff_72_q, j_k_ff_73_q, j_k_ff_74_q, j_k_ff_75_q, j_k_ff_76_q,
       j_k_ff_77_q, j_k_ff_78_q, j_k_ff_79_q, j_k_ff_80_q, j_k_ff_81_q, j_k_ff_82_q, j_k_ff_83_q,
       j_k_ff_84_q, j_k_ff_85_q, j_k_ff_86_q, j_k_ff_87_q, j_k_ff_88_q, j_k_ff_89_q, j_k_ff_90_q,
       j_k_ff_91_q, j_k_ff_92_q, j_k_ff_93_q, j_k_ff_94_q, j_k_ff_95_q, j_k_ff_96_q, j_k_ff_97_q,
       j_k_ff_98_q, j_k_ff_99_q, j_k_ff_100_q, j_k_ff_101_q, j_k_ff_102_q, j_k_ff_103_q, j_k_ff_104_q,
       j_k_ff_105_q, j_k_ff_106_q, j_k_ff_107_q, j_k_ff_108_q, j_k_ff_109_q, j_k_ff_110_q, j_k_ff_111_q,
       j_k_ff_112_q, j_k_ff_113_q, j_k_ff_114_q, j_k_ff_115_q, j_k_ff_116_q, j_k_ff_117_q, j_k_ff_118_q,
       j_k_ff_119_q, j_k_ff_120_q, not_1_out, not_2_out, not_3_out, not_4_out, not_5_out, not_6_out,
       not_7_out, not_8_out, not_9_out, not_10_out, not_11_out, not_12_out, not_13_out, not_14_out,
       not_15_out, not_16_out, not_17_out, not_18_out, not_19_out, not_20_out, not_21_out, not_22_out,
       not_23_out, not_24_out, not_25_out, not_26_out, not_27_out, not_28_out, not_29_out, not_30_out,
       not_31_out, not_32_out, not_33_out, not_34_out, not_35_out, not_36_out, not_37_out, not_38_out,
       not_39_out, not_40_out, not_41_out, not_42_out, not_43_out, not_44_out, not_45_out, not_46_out,
       not_47_out, not_48_out, not_49_out, not_50_out, not_51_out, not_52_out, not_53_out, not_54_out,
       not_55_out, not_56_out, not_57_out, not_58_out, not_59_out, not_60_out, not_61_out, not_62_out,
       not_63_out, not_64_out, not_65_out, not_66_out, not_67_out, not_68_out, not_69_out, not_70_out,
       not_71_out, not_72_out, not_73_out, not_74_out, not_75_out, not_76_out, not_77_out, not_78_out,
       not_79_out, not_80_out, not_81_out, not_82_out, not_83_out, not_84_out, not_85_out, not_86_out,
       not_87_out, not_88_out, not_89_out, not_90_out, not_91_out, not_92_out, not_93_out, not_94_out,
       not_95_out, not_96_out, not_97_out, not_98_out, not_99_out, not_100_out, not_101_out, not_102_out,
       not_103_out, not_104_out, not_105_out, not_106_out, not_107_out, not_108_out, not_109_out,
       not_110_out, not_111_out, not_112_out, not_113_out, not_114_out, not_115_out, not_116_out,
       not_117_out, not_118_out, not_119_out, not_120_out, not_121_out, not_122_out, not_123_out,
       not_124_out, not_125_out, not_126_out, not_127_out, not_128_out;

  Button clear_1 (.out(clear_1_out));
  Button clear_2 (.out(clear_2_out));
  Button clear_3 (.out(clear_3_out));
  Button clear_4 (.out(clear_4_out));
  Button clear_5 (.out(clear_5_out));
  Button clear_6 (.out(clear_6_out));
  Button clear_7 (.out(clear_7_out));
  Button clear_8 (.out(clear_8_out));
  Clock clock__global (.out(clock__global_out));
  not not_1 (not_1_out, entrada_1);
  not not_2 (not_2_out, entrada_2);
  not not_3 (not_3_out, entrada_3);
  not not_4 (not_4_out, entrada_4);
  not not_5 (not_5_out, entrada_5);
  not not_6 (not_6_out, entrada_6);
  not not_7 (not_7_out, entrada_7);
  not not_8 (not_8_out, entrada_8);
  J_K_Flip_Flop j_k_ff_1 (
    .J(entrada_1), .clk(clock__global_out), .K(not_1_out), .Q(j_k_ff_1_q), .reset(clear_1_out));  // open: Qn, preset
  J_K_Flip_Flop j_k_ff_2 (
    .J(entrada_2), .clk(clock__global_out), .K(not_2_out), .Q(j_k_ff_2_q), .reset(clear_2_out));  // open: Qn, preset
  J_K_Flip_Flop j_k_ff_3 (
    .J(entrada_3), .clk(clock__global_out), .K(not_3_out), .Q(j_k_ff_3_q), .reset(clear_3_out));  // open: Qn, preset
  J_K_Flip_Flop j_k_ff_4 (
    .J(entrada_4), .clk(clock__global_out), .K(not_4_out), .Q(j_k_ff_4_q), .reset(clear_4_out));  // open: Qn, preset
  J_K_Flip_Flop j_k_ff_5 (
    .J(entrada_5), .clk(clock__global_out), .K(not_5_out), .Q(j_k_ff_5_q), .reset(clear_5_out));  // open: Qn, preset
  J_K_Flip_Flop j_k_ff_6 (
    .J(entrada_6), .clk(clock__global_out), .K(not_6_out), .Q(j_k_ff_6_q), .reset(clear_6_out));  // open: Qn, preset
  J_K_Flip_Flop j_k_ff_7 (
    .J(entrada_7), .clk(clock__global_out), .K(not_7_out), .Q(j_k_ff_7_q), .reset(clear_7_out));  // open: Qn, preset
  J_K_Flip_Flop j_k_ff_8 (
    .J(entrada_8), .clk(clock__global_out), .K(not_8_out), .Q(j_k_ff_8_q), .reset(clear_8_out));  // open: Qn, preset
  J_K_Flip_Flop j_k_ff_9 (
    .J(j_k_ff_1_q), .clk(clock__global_out), .K(not_9_out), .Q(j_k_ff_9_q), .reset(clear_1_out));  // open: Qn, preset
  not not_9 (not_9_out, j_k_ff_1_q);
  J_K_Flip_Flop j_k_ff_10 (
    .J(j_k_ff_2_q), .clk(clock__global_out), .K(not_10_out), .Q(j_k_ff_10_q), .reset(clear_2_out));  // open: Qn, preset
  not not_10 (not_10_out, j_k_ff_2_q);
  J_K_Flip_Flop j_k_ff_11 (
    .J(j_k_ff_3_q), .clk(clock__global_out), .K(not_11_out), .Q(j_k_ff_11_q), .reset(clear_3_out));  // open: Qn, preset
  not not_11 (not_11_out, j_k_ff_3_q);
  J_K_Flip_Flop j_k_ff_12 (
    .J(j_k_ff_4_q), .clk(clock__global_out), .K(not_12_out), .Q(j_k_ff_12_q), .reset(clear_4_out));  // open: Qn, preset
  not not_12 (not_12_out, j_k_ff_4_q);
  J_K_Flip_Flop j_k_ff_13 (
    .J(j_k_ff_5_q), .clk(clock__global_out), .K(not_13_out), .Q(j_k_ff_13_q), .reset(clear_5_out));  // open: Qn, preset
  not not_13 (not_13_out, j_k_ff_5_q);
  J_K_Flip_Flop j_k_ff_14 (
    .J(j_k_ff_6_q), .clk(clock__global_out), .K(not_14_out), .Q(j_k_ff_14_q), .reset(clear_6_out));  // open: Qn, preset
  not not_14 (not_14_out, j_k_ff_6_q);
  J_K_Flip_Flop j_k_ff_15 (
    .J(j_k_ff_7_q), .clk(clock__global_out), .K(not_15_out), .Q(j_k_ff_15_q), .reset(clear_7_out));  // open: Qn, preset
  not not_15 (not_15_out, j_k_ff_7_q);
  J_K_Flip_Flop j_k_ff_16 (
    .J(j_k_ff_8_q), .clk(clock__global_out), .K(not_16_out), .Q(j_k_ff_16_q), .reset(clear_8_out));  // open: Qn, preset
  not not_16 (not_16_out, j_k_ff_8_q);
  not not_17 (not_17_out, j_k_ff_9_q);
  not not_18 (not_18_out, j_k_ff_10_q);
  not not_19 (not_19_out, j_k_ff_11_q);
  not not_20 (not_20_out, j_k_ff_12_q);
  not not_21 (not_21_out, j_k_ff_13_q);
  not not_22 (not_22_out, j_k_ff_14_q);
  not not_23 (not_23_out, j_k_ff_15_q);
  not not_24 (not_24_out, j_k_ff_16_q);
  J_K_Flip_Flop j_k_ff_17 (
    .J(j_k_ff_9_q), .clk(clock__global_out), .K(not_17_out), .Q(j_k_ff_17_q), .reset(clear_1_out));  // open: Qn, preset
  not not_25 (not_25_out, j_k_ff_17_q);
  J_K_Flip_Flop j_k_ff_18 (
    .J(j_k_ff_10_q), .clk(clock__global_out), .K(not_18_out), .Q(j_k_ff_18_q), .reset(clear_2_out));  // open: Qn, preset
  not not_26 (not_26_out, j_k_ff_18_q);
  J_K_Flip_Flop j_k_ff_19 (
    .J(j_k_ff_11_q), .clk(clock__global_out), .K(not_19_out), .Q(j_k_ff_19_q), .reset(clear_3_out));  // open: Qn, preset
  not not_27 (not_27_out, j_k_ff_19_q);
  J_K_Flip_Flop j_k_ff_20 (
    .J(j_k_ff_12_q), .clk(clock__global_out), .K(not_20_out), .Q(j_k_ff_20_q), .reset(clear_4_out));  // open: Qn, preset
  not not_28 (not_28_out, j_k_ff_20_q);
  J_K_Flip_Flop j_k_ff_21 (
    .J(j_k_ff_13_q), .clk(clock__global_out), .K(not_21_out), .Q(j_k_ff_21_q), .reset(clear_5_out));  // open: Qn, preset
  not not_29 (not_29_out, j_k_ff_21_q);
  J_K_Flip_Flop j_k_ff_22 (
    .J(j_k_ff_14_q), .clk(clock__global_out), .K(not_22_out), .Q(j_k_ff_22_q), .reset(clear_6_out));  // open: Qn, preset
  not not_30 (not_30_out, j_k_ff_22_q);
  J_K_Flip_Flop j_k_ff_23 (
    .J(j_k_ff_15_q), .clk(clock__global_out), .K(not_23_out), .Q(j_k_ff_23_q), .reset(clear_7_out));  // open: Qn, preset
  not not_31 (not_31_out, j_k_ff_23_q);
  J_K_Flip_Flop j_k_ff_24 (
    .J(j_k_ff_16_q), .clk(clock__global_out), .K(not_24_out), .Q(j_k_ff_24_q), .reset(clear_8_out));  // open: Qn, preset
  not not_32 (not_32_out, j_k_ff_24_q);
  J_K_Flip_Flop j_k_ff_25 (
    .J(j_k_ff_17_q), .clk(clock__global_out), .K(not_25_out), .Q(j_k_ff_25_q), .reset(clear_1_out));  // open: Qn, preset
  J_K_Flip_Flop j_k_ff_26 (
    .J(j_k_ff_18_q), .clk(clock__global_out), .K(not_26_out), .Q(j_k_ff_26_q), .reset(clear_2_out));  // open: Qn, preset
  J_K_Flip_Flop j_k_ff_27 (
    .J(j_k_ff_19_q), .clk(clock__global_out), .K(not_27_out), .Q(j_k_ff_27_q), .reset(clear_3_out));  // open: Qn, preset
  J_K_Flip_Flop j_k_ff_28 (
    .J(j_k_ff_20_q), .clk(clock__global_out), .K(not_28_out), .Q(j_k_ff_28_q), .reset(clear_4_out));  // open: Qn, preset
  J_K_Flip_Flop j_k_ff_29 (
    .J(j_k_ff_21_q), .clk(clock__global_out), .K(not_29_out), .Q(j_k_ff_29_q), .reset(clear_5_out));  // open: Qn, preset
  J_K_Flip_Flop j_k_ff_30 (
    .J(j_k_ff_22_q), .clk(clock__global_out), .K(not_30_out), .Q(j_k_ff_30_q), .reset(clear_6_out));  // open: Qn, preset
  J_K_Flip_Flop j_k_ff_31 (
    .J(j_k_ff_23_q), .clk(clock__global_out), .K(not_31_out), .Q(j_k_ff_31_q), .reset(clear_7_out));  // open: Qn, preset
  J_K_Flip_Flop j_k_ff_32 (
    .J(j_k_ff_24_q), .clk(clock__global_out), .K(not_32_out), .Q(j_k_ff_32_q), .reset(clear_8_out));  // open: Qn, preset
  not not_33 (not_33_out, j_k_ff_25_q);
  not not_34 (not_34_out, j_k_ff_26_q);
  not not_35 (not_35_out, j_k_ff_27_q);
  not not_36 (not_36_out, j_k_ff_28_q);
  not not_37 (not_37_out, j_k_ff_29_q);
  not not_38 (not_38_out, j_k_ff_30_q);
  not not_39 (not_39_out, j_k_ff_31_q);
  not not_40 (not_40_out, j_k_ff_32_q);
  J_K_Flip_Flop j_k_ff_33 (
    .J(j_k_ff_25_q), .clk(clock__global_out), .K(not_33_out), .Q(j_k_ff_33_q), .reset(clear_1_out));  // open: Qn, preset
  not not_41 (not_41_out, j_k_ff_33_q);
  J_K_Flip_Flop j_k_ff_34 (
    .J(j_k_ff_26_q), .clk(clock__global_out), .K(not_34_out), .Q(j_k_ff_34_q), .reset(clear_2_out));  // open: Qn, preset
  not not_42 (not_42_out, j_k_ff_34_q);
  J_K_Flip_Flop j_k_ff_35 (
    .J(j_k_ff_27_q), .clk(clock__global_out), .K(not_35_out), .Q(j_k_ff_35_q), .reset(clear_3_out));  // open: Qn, preset
  not not_43 (not_43_out, j_k_ff_35_q);
  J_K_Flip_Flop j_k_ff_36 (
    .J(j_k_ff_28_q), .clk(clock__global_out), .K(not_36_out), .Q(j_k_ff_36_q), .reset(clear_4_out));  // open: Qn, preset
  not not_44 (not_44_out, j_k_ff_36_q);
  J_K_Flip_Flop j_k_ff_37 (
    .J(j_k_ff_29_q), .clk(clock__global_out), .K(not_37_out), .Q(j_k_ff_37_q), .reset(clear_5_out));  // open: Qn, preset
  not not_45 (not_45_out, j_k_ff_37_q);
  J_K_Flip_Flop j_k_ff_38 (
    .J(j_k_ff_30_q), .clk(clock__global_out), .K(not_38_out), .Q(j_k_ff_38_q), .reset(clear_6_out));  // open: Qn, preset
  not not_46 (not_46_out, j_k_ff_38_q);
  J_K_Flip_Flop j_k_ff_39 (
    .J(j_k_ff_31_q), .clk(clock__global_out), .K(not_39_out), .Q(j_k_ff_39_q), .reset(clear_7_out));  // open: Qn, preset
  not not_47 (not_47_out, j_k_ff_39_q);
  J_K_Flip_Flop j_k_ff_40 (
    .J(j_k_ff_32_q), .clk(clock__global_out), .K(not_40_out), .Q(j_k_ff_40_q), .reset(clear_8_out));  // open: Qn, preset
  not not_48 (not_48_out, j_k_ff_40_q);
  J_K_Flip_Flop j_k_ff_41 (
    .J(j_k_ff_33_q), .clk(clock__global_out), .K(not_41_out), .Q(j_k_ff_41_q), .reset(clear_1_out));  // open: Qn, preset
  not not_49 (not_49_out, j_k_ff_41_q);
  J_K_Flip_Flop j_k_ff_42 (
    .J(j_k_ff_34_q), .clk(clock__global_out), .K(not_42_out), .Q(j_k_ff_42_q), .reset(clear_2_out));  // open: Qn, preset
  not not_50 (not_50_out, j_k_ff_42_q);
  J_K_Flip_Flop j_k_ff_43 (
    .J(j_k_ff_35_q), .clk(clock__global_out), .K(not_43_out), .Q(j_k_ff_43_q), .reset(clear_3_out));  // open: Qn, preset
  not not_51 (not_51_out, j_k_ff_43_q);
  J_K_Flip_Flop j_k_ff_44 (
    .J(j_k_ff_36_q), .clk(clock__global_out), .K(not_44_out), .Q(j_k_ff_44_q), .reset(clear_4_out));  // open: Qn, preset
  not not_52 (not_52_out, j_k_ff_44_q);
  J_K_Flip_Flop j_k_ff_45 (
    .J(j_k_ff_37_q), .clk(clock__global_out), .K(not_45_out), .Q(j_k_ff_45_q), .reset(clear_5_out));  // open: Qn, preset
  not not_53 (not_53_out, j_k_ff_45_q);
  J_K_Flip_Flop j_k_ff_46 (
    .J(j_k_ff_38_q), .clk(clock__global_out), .K(not_46_out), .Q(j_k_ff_46_q), .reset(clear_6_out));  // open: Qn, preset
  not not_54 (not_54_out, j_k_ff_46_q);
  J_K_Flip_Flop j_k_ff_47 (
    .J(j_k_ff_39_q), .clk(clock__global_out), .K(not_47_out), .Q(j_k_ff_47_q), .reset(clear_7_out));  // open: Qn, preset
  not not_55 (not_55_out, j_k_ff_47_q);
  J_K_Flip_Flop j_k_ff_48 (
    .J(j_k_ff_40_q), .clk(clock__global_out), .K(not_48_out), .Q(j_k_ff_48_q), .reset(clear_8_out));  // open: Qn, preset
  not not_56 (not_56_out, j_k_ff_48_q);
  J_K_Flip_Flop j_k_ff_49 (
    .J(j_k_ff_41_q), .clk(clock__global_out), .K(not_49_out), .Q(j_k_ff_49_q), .reset(clear_1_out));  // open: Qn, preset
  J_K_Flip_Flop j_k_ff_50 (
    .J(j_k_ff_42_q), .clk(clock__global_out), .K(not_50_out), .Q(j_k_ff_50_q), .reset(clear_2_out));  // open: Qn, preset
  J_K_Flip_Flop j_k_ff_51 (
    .J(j_k_ff_43_q), .clk(clock__global_out), .K(not_51_out), .Q(j_k_ff_51_q), .reset(clear_3_out));  // open: Qn, preset
  J_K_Flip_Flop j_k_ff_52 (
    .J(j_k_ff_44_q), .clk(clock__global_out), .K(not_52_out), .Q(j_k_ff_52_q), .reset(clear_4_out));  // open: Qn, preset
  J_K_Flip_Flop j_k_ff_53 (
    .J(j_k_ff_45_q), .clk(clock__global_out), .K(not_53_out), .Q(j_k_ff_53_q), .reset(clear_5_out));  // open: Qn, preset
  J_K_Flip_Flop j_k_ff_54 (
    .J(j_k_ff_46_q), .clk(clock__global_out), .K(not_54_out), .Q(j_k_ff_54_q), .reset(clear_6_out));  // open: Qn, preset
  J_K_Flip_Flop j_k_ff_55 (
    .J(j_k_ff_47_q), .clk(clock__global_out), .K(not_55_out), .Q(j_k_ff_55_q), .reset(clear_7_out));  // open: Qn, preset
  J_K_Flip_Flop j_k_ff_56 (
    .J(j_k_ff_48_q), .clk(clock__global_out), .K(not_56_out), .Q(j_k_ff_56_q), .reset(clear_8_out));  // open: Qn, preset
  not not_57 (not_57_out, j_k_ff_49_q);
  not not_58 (not_58_out, j_k_ff_50_q);
  not not_59 (not_59_out, j_k_ff_51_q);
  not not_60 (not_60_out, j_k_ff_52_q);
  not not_61 (not_61_out, j_k_ff_53_q);
  not not_62 (not_62_out, j_k_ff_54_q);
  not not_63 (not_63_out, j_k_ff_55_q);
  not not_64 (not_64_out, j_k_ff_56_q);
  J_K_Flip_Flop j_k_ff_57 (
    .J(j_k_ff_49_q), .clk(clock__global_out), .K(not_57_out), .Q(j_k_ff_57_q), .reset(clear_1_out));  // open: Qn, preset
  not not_65 (not_65_out, j_k_ff_57_q);
  J_K_Flip_Flop j_k_ff_58 (
    .J(j_k_ff_50_q), .clk(clock__global_out), .K(not_58_out), .Q(j_k_ff_58_q), .reset(clear_2_out));  // open: Qn, preset
  not not_66 (not_66_out, j_k_ff_58_q);
  J_K_Flip_Flop j_k_ff_59 (
    .J(j_k_ff_51_q), .clk(clock__global_out), .K(not_59_out), .Q(j_k_ff_59_q), .reset(clear_3_out));  // open: Qn, preset
  not not_67 (not_67_out, j_k_ff_59_q);
  J_K_Flip_Flop j_k_ff_60 (
    .J(j_k_ff_52_q), .clk(clock__global_out), .K(not_60_out), .Q(j_k_ff_60_q), .reset(clear_4_out));  // open: Qn, preset
  not not_68 (not_68_out, j_k_ff_60_q);
  J_K_Flip_Flop j_k_ff_61 (
    .J(j_k_ff_53_q), .clk(clock__global_out), .K(not_61_out), .Q(j_k_ff_61_q), .reset(clear_5_out));  // open: Qn, preset
  not not_69 (not_69_out, j_k_ff_61_q);
  J_K_Flip_Flop j_k_ff_62 (
    .J(j_k_ff_54_q), .clk(clock__global_out), .K(not_62_out), .Q(j_k_ff_62_q), .reset(clear_6_out));  // open: Qn, preset
  not not_70 (not_70_out, j_k_ff_62_q);
  J_K_Flip_Flop j_k_ff_63 (
    .J(j_k_ff_55_q), .clk(clock__global_out), .K(not_63_out), .Q(j_k_ff_63_q), .reset(clear_7_out));  // open: Qn, preset
  not not_71 (not_71_out, j_k_ff_63_q);
  J_K_Flip_Flop j_k_ff_64 (
    .J(j_k_ff_56_q), .clk(clock__global_out), .K(not_64_out), .Q(j_k_ff_64_q), .reset(clear_8_out));  // open: Qn, preset
  not not_72 (not_72_out, j_k_ff_64_q);
  J_K_Flip_Flop j_k_ff_65 (
    .J(j_k_ff_57_q), .clk(clock__global_out), .K(not_65_out), .Q(j_k_ff_65_q), .reset(clear_1_out));  // open: Qn, preset
  J_K_Flip_Flop j_k_ff_66 (
    .J(j_k_ff_58_q), .clk(clock__global_out), .K(not_66_out), .Q(j_k_ff_66_q), .reset(clear_2_out));  // open: Qn, preset
  J_K_Flip_Flop j_k_ff_67 (
    .J(j_k_ff_59_q), .clk(clock__global_out), .K(not_67_out), .Q(j_k_ff_67_q), .reset(clear_3_out));  // open: Qn, preset
  J_K_Flip_Flop j_k_ff_68 (
    .J(j_k_ff_60_q), .clk(clock__global_out), .K(not_68_out), .Q(j_k_ff_68_q), .reset(clear_4_out));  // open: Qn, preset
  J_K_Flip_Flop j_k_ff_69 (
    .J(j_k_ff_61_q), .clk(clock__global_out), .K(not_69_out), .Q(j_k_ff_69_q), .reset(clear_5_out));  // open: Qn, preset
  J_K_Flip_Flop j_k_ff_70 (
    .J(j_k_ff_62_q), .clk(clock__global_out), .K(not_70_out), .Q(j_k_ff_70_q), .reset(clear_6_out));  // open: Qn, preset
  J_K_Flip_Flop j_k_ff_71 (
    .J(j_k_ff_63_q), .clk(clock__global_out), .K(not_71_out), .Q(j_k_ff_71_q), .reset(clear_7_out));  // open: Qn, preset
  J_K_Flip_Flop j_k_ff_72 (
    .J(j_k_ff_64_q), .clk(clock__global_out), .K(not_72_out), .Q(j_k_ff_72_q), .reset(clear_8_out));  // open: Qn, preset
  J_K_Flip_Flop j_k_ff_73 (
    .J(j_k_ff_65_q), .clk(clock__global_out), .K(not_73_out), .Q(j_k_ff_73_q), .reset(clear_1_out));  // open: Qn, preset
  not not_73 (not_73_out, j_k_ff_65_q);
  J_K_Flip_Flop j_k_ff_74 (
    .J(j_k_ff_66_q), .clk(clock__global_out), .K(not_74_out), .Q(j_k_ff_74_q), .reset(clear_2_out));  // open: Qn, preset
  not not_74 (not_74_out, j_k_ff_66_q);
  J_K_Flip_Flop j_k_ff_75 (
    .J(j_k_ff_67_q), .clk(clock__global_out), .K(not_75_out), .Q(j_k_ff_75_q), .reset(clear_3_out));  // open: Qn, preset
  not not_75 (not_75_out, j_k_ff_67_q);
  J_K_Flip_Flop j_k_ff_76 (
    .J(j_k_ff_68_q), .clk(clock__global_out), .K(not_76_out), .Q(j_k_ff_76_q), .reset(clear_4_out));  // open: Qn, preset
  not not_76 (not_76_out, j_k_ff_68_q);
  J_K_Flip_Flop j_k_ff_77 (
    .J(j_k_ff_69_q), .clk(clock__global_out), .K(not_77_out), .Q(j_k_ff_77_q), .reset(clear_5_out));  // open: Qn, preset
  not not_77 (not_77_out, j_k_ff_69_q);
  J_K_Flip_Flop j_k_ff_78 (
    .J(j_k_ff_70_q), .clk(clock__global_out), .K(not_78_out), .Q(j_k_ff_78_q), .reset(clear_6_out));  // open: Qn, preset
  not not_78 (not_78_out, j_k_ff_70_q);
  J_K_Flip_Flop j_k_ff_79 (
    .J(j_k_ff_71_q), .clk(clock__global_out), .K(not_79_out), .Q(j_k_ff_79_q), .reset(clear_7_out));  // open: Qn, preset
  not not_79 (not_79_out, j_k_ff_71_q);
  J_K_Flip_Flop j_k_ff_80 (
    .J(j_k_ff_72_q), .clk(clock__global_out), .K(not_80_out), .Q(j_k_ff_80_q), .reset(clear_8_out));  // open: Qn, preset
  not not_80 (not_80_out, j_k_ff_72_q);
  not not_81 (not_81_out, j_k_ff_73_q);
  not not_82 (not_82_out, j_k_ff_74_q);
  not not_83 (not_83_out, j_k_ff_75_q);
  not not_84 (not_84_out, j_k_ff_76_q);
  not not_85 (not_85_out, j_k_ff_77_q);
  not not_86 (not_86_out, j_k_ff_78_q);
  not not_87 (not_87_out, j_k_ff_79_q);
  not not_88 (not_88_out, j_k_ff_80_q);
  J_K_Flip_Flop j_k_ff_81 (
    .J(j_k_ff_73_q), .clk(clock__global_out), .K(not_81_out), .Q(j_k_ff_81_q), .reset(clear_1_out));  // open: Qn, preset
  not not_89 (not_89_out, j_k_ff_81_q);
  J_K_Flip_Flop j_k_ff_82 (
    .J(j_k_ff_74_q), .clk(clock__global_out), .K(not_82_out), .Q(j_k_ff_82_q), .reset(clear_2_out));  // open: Qn, preset
  not not_90 (not_90_out, j_k_ff_82_q);
  J_K_Flip_Flop j_k_ff_83 (
    .J(j_k_ff_75_q), .clk(clock__global_out), .K(not_83_out), .Q(j_k_ff_83_q), .reset(clear_3_out));  // open: Qn, preset
  not not_91 (not_91_out, j_k_ff_83_q);
  J_K_Flip_Flop j_k_ff_84 (
    .J(j_k_ff_76_q), .clk(clock__global_out), .K(not_84_out), .Q(j_k_ff_84_q), .reset(clear_4_out));  // open: Qn, preset
  not not_92 (not_92_out, j_k_ff_84_q);
  J_K_Flip_Flop j_k_ff_85 (
    .J(j_k_ff_77_q), .clk(clock__global_out), .K(not_85_out), .Q(j_k_ff_85_q), .reset(clear_5_out));  // open: Qn, preset
  not not_93 (not_93_out, j_k_ff_85_q);
  J_K_Flip_Flop j_k_ff_86 (
    .J(j_k_ff_78_q), .clk(clock__global_out), .K(not_86_out), .Q(j_k_ff_86_q), .reset(clear_6_out));  // open: Qn, preset
  not not_94 (not_94_out, j_k_ff_86_q);
  J_K_Flip_Flop j_k_ff_87 (
    .J(j_k_ff_79_q), .clk(clock__global_out), .K(not_87_out), .Q(j_k_ff_87_q), .reset(clear_7_out));  // open: Qn, preset
  not not_95 (not_95_out, j_k_ff_87_q);
  J_K_Flip_Flop j_k_ff_88 (
    .J(j_k_ff_80_q), .clk(clock__global_out), .K(not_88_out), .Q(j_k_ff_88_q), .reset(clear_8_out));  // open: Qn, preset
  not not_96 (not_96_out, j_k_ff_88_q);
  J_K_Flip_Flop j_k_ff_89 (
    .J(j_k_ff_81_q), .clk(clock__global_out), .K(not_89_out), .Q(j_k_ff_89_q), .reset(clear_1_out));  // open: Qn, preset
  J_K_Flip_Flop j_k_ff_90 (
    .J(j_k_ff_82_q), .clk(clock__global_out), .K(not_90_out), .Q(j_k_ff_90_q), .reset(clear_2_out));  // open: Qn, preset
  J_K_Flip_Flop j_k_ff_91 (
    .J(j_k_ff_83_q), .clk(clock__global_out), .K(not_91_out), .Q(j_k_ff_91_q), .reset(clear_3_out));  // open: Qn, preset
  J_K_Flip_Flop j_k_ff_92 (
    .J(j_k_ff_84_q), .clk(clock__global_out), .K(not_92_out), .Q(j_k_ff_92_q), .reset(clear_4_out));  // open: Qn, preset
  J_K_Flip_Flop j_k_ff_93 (
    .J(j_k_ff_85_q), .clk(clock__global_out), .K(not_93_out), .Q(j_k_ff_93_q), .reset(clear_5_out));  // open: Qn, preset
  J_K_Flip_Flop j_k_ff_94 (
    .J(j_k_ff_86_q), .clk(clock__global_out), .K(not_94_out), .Q(j_k_ff_94_q), .reset(clear_6_out));  // open: Qn, preset
  J_K_Flip_Flop j_k_ff_95 (
    .J(j_k_ff_87_q), .clk(clock__global_out), .K(not_95_out), .Q(j_k_ff_95_q), .reset(clear_7_out));  // open: Qn, preset
  J_K_Flip_Flop j_k_ff_96 (
    .J(j_k_ff_88_q), .clk(clock__global_out), .K(not_96_out), .Q(j_k_ff_96_q), .reset(clear_8_out));  // open: Qn, preset
  not not_97 (not_97_out, j_k_ff_89_q);
  not not_98 (not_98_out, j_k_ff_90_q);
  not not_99 (not_99_out, j_k_ff_91_q);
  not not_100 (not_100_out, j_k_ff_92_q);
  not not_101 (not_101_out, j_k_ff_93_q);
  not not_102 (not_102_out, j_k_ff_94_q);
  not not_103 (not_103_out, j_k_ff_95_q);
  not not_104 (not_104_out, j_k_ff_96_q);
  J_K_Flip_Flop j_k_ff_97 (
    .J(j_k_ff_89_q), .clk(clock__global_out), .K(not_97_out), .Q(j_k_ff_97_q), .reset(clear_1_out));  // open: Qn, preset
  not not_105 (not_105_out, j_k_ff_97_q);
  J_K_Flip_Flop j_k_ff_98 (
    .J(j_k_ff_90_q), .clk(clock__global_out), .K(not_98_out), .Q(j_k_ff_98_q), .reset(clear_2_out));  // open: Qn, preset
  not not_106 (not_106_out, j_k_ff_98_q);
  J_K_Flip_Flop j_k_ff_99 (
    .J(j_k_ff_91_q), .clk(clock__global_out), .K(not_99_out), .Q(j_k_ff_99_q), .reset(clear_3_out));  // open: Qn, preset
  not not_107 (not_107_out, j_k_ff_99_q);
  J_K_Flip_Flop j_k_ff_100 (
    .J(j_k_ff_92_q), .clk(clock__global_out), .K(not_100_out), .Q(j_k_ff_100_q), .reset(clear_4_out));  // open: Qn, preset
  not not_108 (not_108_out, j_k_ff_100_q);
  J_K_Flip_Flop j_k_ff_101 (
    .J(j_k_ff_93_q), .clk(clock__global_out), .K(not_101_out), .Q(j_k_ff_101_q), .reset(clear_5_out));  // open: Qn, preset
  not not_109 (not_109_out, j_k_ff_101_q);
  J_K_Flip_Flop j_k_ff_102 (
    .J(j_k_ff_94_q), .clk(clock__global_out), .K(not_102_out), .Q(j_k_ff_102_q), .reset(clear_6_out));  // open: Qn, preset
  not not_110 (not_110_out, j_k_ff_102_q);
  J_K_Flip_Flop j_k_ff_103 (
    .J(j_k_ff_95_q), .clk(clock__global_out), .K(not_103_out), .Q(j_k_ff_103_q), .reset(clear_7_out));  // open: Qn, preset
  not not_111 (not_111_out, j_k_ff_103_q);
  J_K_Flip_Flop j_k_ff_104 (
    .J(j_k_ff_96_q), .clk(clock__global_out), .K(not_104_out), .Q(j_k_ff_104_q), .reset(clear_8_out));  // open: Qn, preset
  not not_112 (not_112_out, j_k_ff_104_q);
  J_K_Flip_Flop j_k_ff_105 (
    .J(j_k_ff_97_q), .clk(clock__global_out), .K(not_105_out), .Q(j_k_ff_105_q), .reset(clear_1_out));  // open: Qn, preset
  not not_113 (not_113_out, j_k_ff_105_q);
  J_K_Flip_Flop j_k_ff_106 (
    .J(j_k_ff_98_q), .clk(clock__global_out), .K(not_106_out), .Q(j_k_ff_106_q), .reset(clear_2_out));  // open: Qn, preset
  not not_114 (not_114_out, j_k_ff_106_q);
  J_K_Flip_Flop j_k_ff_107 (
    .J(j_k_ff_99_q), .clk(clock__global_out), .K(not_107_out), .Q(j_k_ff_107_q), .reset(clear_3_out));  // open: Qn, preset
  not not_115 (not_115_out, j_k_ff_107_q);
  J_K_Flip_Flop j_k_ff_108 (
    .J(j_k_ff_100_q), .clk(clock__global_out), .K(not_108_out), .Q(j_k_ff_108_q), .reset(clear_4_out));  // open: Qn, preset
  not not_116 (not_116_out, j_k_ff_108_q);
  J_K_Flip_Flop j_k_ff_109 (
    .J(j_k_ff_101_q), .clk(clock__global_out), .K(not_109_out), .Q(j_k_ff_109_q), .reset(clear_5_out));  // open: Qn, preset
  not not_117 (not_117_out, j_k_ff_109_q);
  J_K_Flip_Flop j_k_ff_110 (
    .J(j_k_ff_102_q), .clk(clock__global_out), .K(not_110_out), .Q(j_k_ff_110_q), .reset(clear_6_out));  // open: Qn, preset
  not not_118 (not_118_out, j_k_ff_110_q);
  J_K_Flip_Flop j_k_ff_111 (
    .J(j_k_ff_103_q), .clk(clock__global_out), .K(not_111_out), .Q(j_k_ff_111_q), .reset(clear_7_out));  // open: Qn, preset
  not not_119 (not_119_out, j_k_ff_111_q);
  J_K_Flip_Flop j_k_ff_112 (
    .J(j_k_ff_104_q), .clk(clock__global_out), .K(not_112_out), .Q(j_k_ff_112_q), .reset(clear_8_out));  // open: Qn, preset
  not not_120 (not_120_out, j_k_ff_112_q);
  J_K_Flip_Flop j_k_ff_113 (
    .J(j_k_ff_105_q), .clk(clock__global_out), .K(not_113_out), .Q(j_k_ff_113_q), .reset(clear_1_out));  // open: Qn, preset
  J_K_Flip_Flop j_k_ff_114 (
    .J(j_k_ff_106_q), .clk(clock__global_out), .K(not_114_out), .Q(j_k_ff_114_q), .reset(clear_2_out));  // open: Qn, preset
  J_K_Flip_Flop j_k_ff_115 (
    .J(j_k_ff_107_q), .clk(clock__global_out), .K(not_115_out), .Q(j_k_ff_115_q), .reset(clear_3_out));  // open: Qn, preset
  J_K_Flip_Flop j_k_ff_116 (
    .J(j_k_ff_108_q), .clk(clock__global_out), .K(not_116_out), .Q(j_k_ff_116_q), .reset(clear_4_out));  // open: Qn, preset
  J_K_Flip_Flop j_k_ff_117 (
    .J(j_k_ff_109_q), .clk(clock__global_out), .K(not_117_out), .Q(j_k_ff_117_q), .reset(clear_5_out));  // open: Qn, preset
  J_K_Flip_Flop j_k_ff_118 (
    .J(j_k_ff_110_q), .clk(clock__global_out), .K(not_118_out), .Q(j_k_ff_118_q), .reset(clear_6_out));  // open: Qn, preset
  J_K_Flip_Flop j_k_ff_119 (
    .J(j_k_ff_111_q), .clk(clock__global_out), .K(not_119_out), .Q(j_k_ff_119_q), .reset(clear_7_out));  // open: Qn, preset
  J_K_Flip_Flop j_k_ff_120 (
    .J(j_k_ff_112_q), .clk(clock__global_out), .K(not_120_out), .Q(j_k_ff_120_q), .reset(clear_8_out));  // open: Qn, preset
  not not_121 (not_121_out, j_k_ff_113_q);
  not not_122 (not_122_out, j_k_ff_114_q);
  not not_123 (not_123_out, j_k_ff_115_q);
  not not_124 (not_124_out, j_k_ff_116_q);
  not not_125 (not_125_out, j_k_ff_117_q);
  not not_126 (not_126_out, j_k_ff_118_q);
  not not_127 (not_127_out, j_k_ff_119_q);
  not not_128 (not_128_out, j_k_ff_120_q);
  J_K_Flip_Flop j_k_ff_121 (
    .J(j_k_ff_113_q), .clk(clock__global_out), .K(not_121_out), .reset(clear_1_out));  // open: Q, Qn, preset
  J_K_Flip_Flop j_k_ff_122 (
    .J(j_k_ff_114_q), .clk(clock__global_out), .K(not_122_out), .reset(clear_2_out));  // open: Q, Qn, preset
  J_K_Flip_Flop j_k_ff_123 (
    .J(j_k_ff_115_q), .clk(clock__global_out), .K(not_123_out), .reset(clear_3_out));  // open: Q, Qn, preset
  J_K_Flip_Flop j_k_ff_124 (
    .J(j_k_ff_116_q), .clk(clock__global_out), .K(not_124_out), .reset(clear_4_out));  // open: Q, Qn, preset
  J_K_Flip_Flop j_k_ff_125 (
    .J(j_k_ff_117_q), .clk(clock__global_out), .K(not_125_out), .reset(clear_5_out));  // open: Q, Qn, preset
  J_K_Flip_Flop j_k_ff_126 (
    .J(j_k_ff_118_q), .clk(clock__global_out), .K(not_126_out), .reset(clear_6_out));  // open: Q, Qn, preset
  J_K_Flip_Flop j_k_ff_127 (
    .J(j_k_ff_119_q), .clk(clock__global_out), .K(not_127_out), .reset(clear_7_out));  // open: Q, Qn, preset
  J_K_Flip_Flop j_k_ff_128 (
    .J(j_k_ff_120_q), .clk(clock__global_out), .K(not_128_out), .reset(clear_8_out));  // open: Q, Qn, preset
endmodule
