// Logisim project G1302.circ as structural Verilog: 1 circuit, main circuit main
module main (
  output out_1,
  output out_2,
  output out_3,
  output out_4,
  output out_5,
  output out_6
);

  wire _2_0_qn, _2_1_qn, _2_2_qn, _2_3_qn, _2_4_qn, Clock_out, Reset__1_out;

  Clock Clock (.out(Clock_out));
  Button Reset__1 (.out(Reset__1_out));
  J_K_Flip_Flop _2_5 (.J(1'b1), .clk(_2_4_qn), .K(1'b1), .Q(out_1), .reset(Reset__1_out));  // open: Qn, preset
  J_K_Flip_Flop _2_4 (
    .J(1'b1), .clk(_2_3_qn), .K(1'b1), .Q(out_2), .Qn(_2_4_qn), .reset(Reset__1_out));  // open: preset
  J_K_Flip_Flop _2_3 (
    .J(1'b1), .clk(_2_2_qn), .K(1'b1), .Q(out_3), .Qn(_2_3_qn), .reset(Reset__1_out));  // open: preset
  J_K_Flip_Flop _2_2 (
    .J(1'b1), .clk(_2_1_qn), .K(1'b1), .Q(out_4), .Qn(_2_2_qn), .reset(Reset__1_out));  // open: preset
  J_K_Flip_Flop _2_1 (
    .J(1'b1), .clk(_2_0_qn), .K(1'b1), .Q(out_5), .Qn(_2_1_qn), .reset(Reset__1_out));  // open: preset
  J_K_Flip_Flop _2_0 (
    .J(1'b1), .clk(Clock_out), .K(1'b1), .Q(out_6), .Qn(_2_0_qn), .reset(Reset__1_out));  // open: preset
endmodule
