// Logisim project G1307.circ as structural Verilog: 1 circuit, main circuit main
module main (
  output out_1,
  output out_2,
  output out_3,
  output out_4,
  output out_5,
  output out_6
);

  wire and_1_out, clock_1_out, not_1_out, not_2_out, not_3_out, not_4_out, not_5_out, not_6_out, not_7_out,
       Reset_out;

  Clock clock_1 (.out(clock_1_out));
  not not_1 (not_1_out, out_6);
  Button Reset (.out(Reset_out));
  and and_1 (and_1_out, not_1_out, 1'b1);
  not not_2 (not_2_out, and_1_out);
  J_K_Flip_Flop j_k_ff_1 (
    .J(and_1_out), .clk(clock_1_out), .K(not_2_out), .Q(out_1), .reset(Reset_out));  // open: Qn, preset
  not not_3 (not_3_out, out_1);
  J_K_Flip_Flop j_k_ff_2 (
    .J(out_1), .clk(clock_1_out), .K(not_3_out), .Q(out_2), .reset(Reset_out));  // open: Qn, preset
  not not_4 (not_4_out, out_2);
  J_K_Flip_Flop j_k_ff_3 (
    .J(out_2), .clk(clock_1_out), .K(not_4_out), .Q(out_3), .reset(Reset_out));  // open: Qn, preset
  not not_5 (not_5_out, out_3);
  J_K_Flip_Flop j_k_ff_4 (
    .J(out_3), .clk(clock_1_out), .K(not_5_out), .Q(out_4), .reset(Reset_out));  // open: Qn, preset
  not not_6 (not_6_out, out_4);
  J_K_Flip_Flop j_k_ff_5 (
    .J(out_4), .clk(clock_1_out), .K(not_6_out), .Q(out_5), .reset(Reset_out));  // open: Qn, preset
  not not_7 (not_7_out, out_5);
  J_K_Flip_Flop j_k_ff_6 (
    .J(out_5), .clk(clock_1_out), .K(not_7_out), .Q(out_6), .reset(Reset_out));  // open: Qn, preset
endmodule
