// Logisim project G1402.circ as structural Verilog: 1 circuit, main circuit main
module main (
  input  in_1,
  input  Entrada_Paralela_1,
  input  Entrada_Paralela_2,
  input  Entrada_Paralela_3,
  input  Entrada_Paralela_4,
  input  Entrada_Paralela_5,
  output out_7,
  output out_8,
  output out_9,
  output out_10,
  output out_11
);

  wire and_1_out, and_2_out, and_3_out, and_4_out, and_5_out, and_6_out, and_7_out, and_8_out, and_9_out,
       Clear_out, \Clock__Ler_Avançar_out , not_1_out, not_2_out, not_3_out, not_4_out, not_5_out, or_1_out,
       or_2_out, or_3_out, or_4_out, or_5_out;

  Clock \Clock__Ler_Avançar  (.out(\Clock__Ler_Avançar_out ));
  Button Clear (.out(Clear_out));
  not not_1 (not_1_out, in_1);
  and and_1 (and_1_out, not_1_out, out_8);
  or or_1 (or_1_out, and_1_out, and_2_out);
  and and_2 (and_2_out, in_1, Entrada_Paralela_1);
  not not_2 (not_2_out, in_1);
  D_Flip_Flop d_ff_1 (.clk(\Clock__Ler_Avançar_out ), .D(or_1_out), .Q(out_7), .reset(Clear_out));  // open: Qn, preset
  and and_3 (and_3_out, not_2_out, out_9);
  or or_2 (or_2_out, and_3_out, and_4_out);
  and and_4 (and_4_out, in_1, Entrada_Paralela_2);
  not not_3 (not_3_out, in_1);
  D_Flip_Flop d_ff_2 (.clk(\Clock__Ler_Avançar_out ), .D(or_2_out), .Q(out_8), .reset(Clear_out));  // open: Qn, preset
  and and_5 (and_5_out, not_3_out, out_10);
  and and_6 (and_6_out, in_1, Entrada_Paralela_3);
  or or_3 (or_3_out, and_5_out, and_6_out);
  not not_4 (not_4_out, in_1);
  D_Flip_Flop d_ff_3 (.clk(\Clock__Ler_Avançar_out ), .D(or_3_out), .Q(out_9), .reset(Clear_out));  // open: Qn, preset
  and and_7 (and_7_out, not_4_out, out_11);
  and and_8 (and_8_out, in_1, Entrada_Paralela_4);
  D_Flip_Flop d_ff_4 (.clk(\Clock__Ler_Avançar_out ), .D(or_4_out), .Q(out_10), .reset(Clear_out));  // open: Qn, preset
  or or_4 (or_4_out, and_7_out, and_8_out);
  not not_5 (not_5_out, in_1);
  or or_5 (or_5_out, not_5_out, and_9_out);
  and and_9 (and_9_out, in_1, Entrada_Paralela_5);
  D_Flip_Flop d_ff_5 (.clk(\Clock__Ler_Avançar_out ), .D(or_5_out), .Q(out_11), .reset(Clear_out));  // open: Qn, preset

  // Notes on the sheet:
  //   1 + Clock = Leitura Paralela
  //   0 + Clock = Avanço para esquerda
endmodule
