// Logisim project G1403.circ as structural Verilog: 1 circuit, main circuit main
module main (
  output out_1,
  output out_2,
  output out_3,
  output out_4,
  output out_5
);

  wire and_1_out, Clock_out, not_1_out, not_2_out, not_3_out, not_4_out, not_5_out, or_1_out, Reset_out;

  Clock Clock (.out(Clock_out));
  or or_1 (or_1_out, and_1_out, out_5);
  not not_1 (not_1_out, out_1);
  not not_2 (not_2_out, out_2);
  and and_1 (and_1_out, not_1_out, not_2_out, not_3_out, not_4_out, not_5_out);
  not not_3 (not_3_out, out_3);
  not not_4 (not_4_out, out_4);
  not not_5 (not_5_out, out_5);
  Button Reset (.out(Reset_out));
  D_Flip_Flop d_ff_1 (.clk(Clock_out), .D(or_1_out), .Q(out_1), .reset(Reset_out));  // open: Qn, preset
  D_Flip_Flop d_ff_2 (.clk(Clock_out), .D(out_1), .Q(out_2), .reset(Reset_out));  // open: Qn, preset
  D_Flip_Flop d_ff_3 (.clk(Clock_out), .D(out_2), .Q(out_3), .reset(Reset_out));  // open: Qn, preset
  D_Flip_Flop d_ff_4 (.clk(Clock_out), .D(out_3), .Q(out_4), .reset(Reset_out));  // open: Qn, preset
  D_Flip_Flop d_ff_5 (.clk(Clock_out), .D(out_4), .Q(out_5), .reset(Reset_out));  // open: Qn, preset
endmodule
