// Logisim project G1404.circ as structural Verilog: 1 circuit, main circuit main
module main (
  output out_1,
  output out_2,
  output out_3,
  output out_4,
  output out_5
);

  wire Clock_out, not_1_out, Reset_out;

  Clock Clock (.out(Clock_out));
  not not_1 (not_1_out, out_1);
  Button Reset (.out(Reset_out));
  D_Flip_Flop d_ff_1 (.clk(Clock_out), .D(not_1_out), .Q(out_5), .reset(Reset_out));  // open: Qn, preset
  D_Flip_Flop d_ff_2 (.clk(Clock_out), .D(out_5), .Q(out_4), .reset(Reset_out));  // open: Qn, preset
  D_Flip_Flop d_ff_3 (.clk(Clock_out), .D(out_4), .Q(out_3), .reset(Reset_out));  // open: Qn, preset
  D_Flip_Flop d_ff_4 (.clk(Clock_out), .D(out_3), .Q(out_2), .reset(Reset_out));  // open: Qn, preset
  D_Flip_Flop d_ff_5 (.clk(Clock_out), .D(out_2), .Q(out_1), .reset(Reset_out));  // open: Qn, preset
endmodule
