// Logisim project Q06.circ as structural Verilog: 1 circuit, main circuit main
module main (
  input  in_1,
  output Q1,
  output Q2,
  output Q3
);

  wire clock_1_out, not_1_out, not_2_out, not_3_out;

  Clock clock_1 (.out(clock_1_out));
  not not_1 (not_1_out, in_1);
  J_K_Flip_Flop j_k_ff_1 (.J(in_1), .clk(clock_1_out), .K(not_1_out), .Q(Q1));  // open: Qn, preset, reset
  not not_2 (not_2_out, Q1);
  J_K_Flip_Flop j_k_ff_2 (.J(Q1), .clk(clock_1_out), .K(not_2_out), .Q(Q2));  // open: Qn, preset, reset
  not not_3 (not_3_out, Q2);
  J_K_Flip_Flop j_k_ff_3 (.J(Q2), .clk(clock_1_out), .K(not_3_out), .Q(in_1));  // open: Qn, preset, reset

  assign Q3 = in_1;
endmodule
