// Logisim project exercicio2_1.circ as structural Verilog: 5 circuits, main circuit Ula
module Ula (
  input  b_invert,
  input  carry_in,
  input  a,
  input  SL1,
  input  SL0,
  input  b,
  output Result,
  output carry_out
);

  wire and_1_out, not_1_out, or_1_out, soma_s, xor_1_out;

  xor xor_1 (xor_1_out, b_invert, b);
  and and_1 (and_1_out, a, xor_1_out);
  or or_1 (or_1_out, a, xor_1_out);
  not not_1 (not_1_out, a);
  soma soma (.A(a), .B(xor_1_out), .C(carry_in), .vai_um(carry_out), .S(soma_s));
  operation Operation (
    .a_and_b(and_1_out), .a_or_b(or_1_out), .not_a(not_1_out), .a_sum_b(soma_s), .OP1(SL1), .OP0(SL0),
    .\saída (Result));
endmodule

module soma (
  input  A,
  input  C,
  input  B,
  output S,
  output vai_um
);

  wire meia_soma_1_s, meia_soma_1_vai_um, meia_soma_2_vai_um;

  meia_soma meia_soma_1 (.A(A), .B(B), .S(meia_soma_1_s), .Vai_um(meia_soma_1_vai_um));
  meia_soma meia_soma_2 (.A(meia_soma_1_s), .B(C), .S(S), .Vai_um(meia_soma_2_vai_um));
  or or_1 (vai_um, meia_soma_1_vai_um, meia_soma_2_vai_um);
endmodule

module meia_soma (
  input  A,
  input  B,
  output S,
  output Vai_um
);

  xor xor_1 (S, B, A);
  and and_1 (Vai_um, B, A);

  // Notes on the sheet:
  //   Meia soma
endmodule

module Ula_4bits (
  input  b3,
  input  b2,
  input  b1,
  input  b0,
  input  a3,
  input  a2,
  input  a1,
  input  a0,
  input  b_invert,
  input  OP1,
  input  OP2,
  output S0,
  output S1,
  output S2,
  output S3,
  output C_out
);

  wire ula_1_carry_out, ula_2_carry_out, ula_3_carry_out;

  Ula ula_1 (
    .a(a0), .b(b0), .b_invert(b_invert), .carry_in(b_invert), .SL1(OP1), .SL0(OP2),
    .carry_out(ula_1_carry_out), .Result(S0));
  Ula ula_2 (
    .a(a1), .b(b1), .b_invert(b_invert), .carry_in(ula_1_carry_out), .SL1(OP1), .SL0(OP2),
    .carry_out(ula_2_carry_out), .Result(S1));
  Ula ula_3 (
    .a(a2), .b(b2), .b_invert(b_invert), .carry_in(ula_2_carry_out), .SL1(OP1), .SL0(OP2),
    .carry_out(ula_3_carry_out), .Result(S2));
  Ula ula_4 (
    .a(a3), .b(b3), .b_invert(b_invert), .carry_in(ula_3_carry_out), .SL1(OP1), .SL0(OP2), .carry_out(C_out),
    .Result(S3));

  // Notes on the sheet:
  //   00 = a and b
  //   01 = a or b
  //   10 = not a
  //   11 = a sum b
endmodule

module operation (
  input  a_and_b,
  input  OP1,
  input  OP0,
  input  a_or_b,
  input  not_a,
  input  a_sum_b,
  output \saída 
);

  Multiplexer #(.select(2), .enable("false")) multiplexer_1 (
    .in0(a_and_b), .in1(a_or_b), .in2(not_a), .in3(a_sum_b), .out(\saída ), .sel({OP1, OP0}));
endmodule
