// Logisim project exercicio2_2.circ as structural Verilog: 5 circuits, main circuit soma
module soma (
  input  A,
  input  C,
  input  B,
  output S,
  output vai_um
);

  wire meia_soma_1_s, meia_soma_1_vai_um, meia_soma_2_vai_um;

  meia_soma meia_soma_1 (.A(A), .B(B), .S(meia_soma_1_s), .Vai_um(meia_soma_1_vai_um));
  meia_soma meia_soma_2 (.A(meia_soma_1_s), .B(C), .S(S), .Vai_um(meia_soma_2_vai_um));
  or or_1 (vai_um, meia_soma_1_vai_um, meia_soma_2_vai_um);
endmodule

module meia_soma (
  input  A,
  input  B,
  output S,
  output Vai_um
);

  xor xor_1 (S, B, A);
  and and_1 (Vai_um, B, A);

  // Notes on the sheet:
  //   Meia soma
endmodule

module NovaUla (
  input  B,
  input  A,
  input  S3,
  input  S2,
  input  S1,
  input  S0,
  input  CI,
  input  M,
  output \Saída ,
  output CO
);

  wire and_1_out, and_2_out, and_3_out, and_4_out, and_5_out, not_1_out, not_2_out, not_3_out, not_4_out,
       not_5_out, not_6_out, not_7_out, not_8_out, not_9_out, not_10_out, novooperation_1_saida, or_1_out,
       or_2_out, or_3_out, or_4_out, xor_1_out, xor_2_out;

  or or_1 (or_1_out, B, A);
  not not_1 (not_1_out, A);
  and and_1 (and_1_out, B, A);
  not not_2 (not_2_out, B);
  not not_3 (not_3_out, A);
  xor xor_1 (xor_1_out, B, A);
  not not_4 (not_4_out, B);
  not not_5 (not_5_out, A);
  not not_6 (not_6_out, or_1_out);
  and and_2 (and_2_out, not_1_out, B);
  not not_7 (not_7_out, and_1_out);
  not not_8 (not_8_out, B);
  xor xor_2 (xor_2_out, B, A);
  and and_3 (and_3_out, not_2_out, A);
  or or_2 (or_2_out, B, not_3_out);
  not not_9 (not_9_out, xor_1_out);
  and and_4 (and_4_out, B, A);
  or or_3 (or_3_out, not_4_out, A);
  or or_4 (or_4_out, B, A);
  NovoOperation novooperation_1 (
    .E0(not_5_out), .E1(not_6_out), .E2(and_2_out), .E3(1'b0), .E4(not_7_out), .E5(not_8_out),
    .E6(xor_2_out), .E7(and_3_out), .E8(or_2_out), .E9(not_9_out), .EA(B), .EB(and_4_out), .EC(1'b1),
    .ED(or_3_out), .EE(or_4_out), .EF(A), .S3(S3), .S2(S2), .S1(S1), .S0(S0), .saida(novooperation_1_saida));
  soma soma_1 (.A(and_5_out), .B(novooperation_1_saida), .C(1'b0), .vai_um(CO), .S(\Saída ));
  not not_10 (not_10_out, M);
  and and_5 (and_5_out, CI, not_10_out);

  // Notes on the sheet:
  //   ULA
endmodule

module NovoOperation (
  input  E0,
  input  E1,
  input  E2,
  input  E3,
  input  S3,
  input  S2,
  input  S1,
  input  S0,
  input  E4,
  input  E5,
  input  E6,
  input  E7,
  input  E8,
  input  E9,
  input  EA,
  input  EB,
  input  EC,
  input  ED,
  input  EE,
  input  EF,
  output saida
);

  Multiplexer #(.select(4), .enable("false")) multiplexer_1 (
    .in0(E0), .in1(E1), .in2(E2), .in3(E3), .in4(E4), .in5(E5), .in6(E6), .in7(E7), .in8(E8), .in9(E9),
    .in10(EA), .in11(EB), .in12(EC), .in13(ED), .in14(EE), .in15(EF), .out(saida), .sel({S3, S2, S1, S0}));

  // Notes on the sheet:
  //   Operation
endmodule

module NovaUla_4bits (
  input  C,
  input  M,
  input  O3,
  input  O2,
  input  O1,
  input  O0,
  input  A3,
  input  A2,
  input  A1,
  input  A0,
  input  B3,
  input  B2,
  input  B1,
  input  B0,
  output S0,
  output S1,
  output S2,
  output S3
);

  wire novaula_1_co, novaula_2_co, novaula_3_co;

  NovaUla novaula_1 (
    .B(A0), .A(A0), .S3(O3), .S2(O2), .S1(O1), .S0(O0), .CI(C), .M(M), .CO(novaula_1_co), .\Saída (S0));
  NovaUla novaula_2 (
    .B(B1), .A(A1), .S3(O3), .S2(O2), .S1(O1), .S0(O0), .CI(novaula_1_co), .M(M), .CO(novaula_2_co),
    .\Saída (S1));
  NovaUla novaula_3 (
    .B(B2), .A(A2), .S3(O3), .S2(O2), .S1(O1), .S0(O0), .CI(novaula_2_co), .M(M), .CO(novaula_3_co),
    .\Saída (S2));
  NovaUla novaula_4 (
    .B(B3), .A(A3), .S3(O3), .S2(O2), .S1(O1), .S0(O0), .CI(novaula_3_co), .M(M), .\Saída (S3));  // open: CO

  assign B0 = A0;

  // Notes on the sheet:
  //   M(H) = Sem Carry
  //   M(L) = Com Carry
endmodule
