// Logisim project LogsimG0602.circ as structural Verilog: 1 circuit, main circuit main
module main (
  input  x,
  input  y,
  input  z,
  input  x_2,
  input  y_2,
  input  z_2,
  input  x_3,
  input  y_3,
  input  z_3,
  input  x_4,
  input  y_4,
  input  z_4,
  input  x_5,
  input  y_5,
  input  z_5,
  output out_16,
  output out_17,
  output out_18,
  output out_19,
  output out_20
);

  wire and_1_out, and_2_out, and_3_out, and_4_out, and_5_out, and_6_out, and_7_out, and_9_out, and_10_out,
       not_1_out, not_2_out, not_3_out, not_4_out, not_5_out, not_6_out, not_7_out, not_8_out, not_9_out,
       not_10_out, not_11_out, or_1_out, or_2_out, or_3_out;

  not not_1 (not_1_out, z_4);
  not not_2 (not_2_out, y_4);
  not not_3 (not_3_out, x_4);
  not not_4 (not_4_out, y_5);
  not not_5 (not_5_out, x_5);
  not not_6 (not_6_out, z);
  and and_1 (and_1_out, y, not_7_out);
  not not_7 (not_7_out, x);
  and and_2 (and_2_out, y_2, not_8_out);
  not not_8 (not_8_out, x_2);
  and and_3 (and_3_out, z_3, x_3);
  not not_9 (not_9_out, z_3);
  and and_4 (and_4_out, not_9_out, not_10_out);
  not not_10 (not_10_out, y_3);
  and and_5 (and_5_out, z_4, y_4);
  or or_1 (or_1_out, and_5_out, not_1_out);
  and and_6 (and_6_out, not_2_out, x_4);
  or or_2 (or_2_out, and_6_out, and_7_out);
  and and_7 (and_7_out, y_4, not_3_out);
  or or_3 (or_3_out, not_4_out, not_5_out);
  not not_11 (not_11_out, z_5);
  or or_4 (out_16, not_6_out, and_1_out);
  or or_5 (out_17, z_2, and_2_out);
  or or_6 (out_18, and_3_out, and_4_out);
  and and_8 (out_19, or_1_out, or_2_out);
  and and_9 (and_9_out, z_5, or_3_out);
  or or_7 (out_20, and_9_out, and_10_out);
  and and_10 (and_10_out, not_11_out, y_5, x_5);

  // Notes on the sheet:
  //   Letra a)
  //   Letra b)
  //   Letra c)
  //   Letra d)
  //   Letra e)
endmodule
