// Logisim project G1203.circ as structural Verilog: 1 circuit, main circuit main
module main (
  input  entrada_1,
  input  entrada_2
);

  wire clear_1_out, clear_2_out, clock_1_out, clock_2_out, j_k_ff_1_q, j_k_ff_2_q, j_k_ff_3_q, j_k_ff_4_q,
       j_k_ff_5_q, j_k_ff_6_q, j_k_ff_7_q, j_k_ff_8_q, j_k_ff_9_q, j_k_ff_10_q, j_k_ff_11_q, j_k_ff_12_q,
       j_k_ff_13_q, j_k_ff_14_q, not_1_out, not_2_out, not_3_out, not_4_out, not_5_out, not_6_out, not_7_out,
       not_8_out, not_9_out, not_10_out, not_11_out, not_12_out, not_13_out, not_14_out, not_15_out,
       not_16_out;

  Button clear_1 (.out(clear_1_out));
  Button clear_2 (.out(clear_2_out));
  Clock clock_1 (.out(clock_1_out));
  not not_1 (not_1_out, entrada_1);
  Clock clock_2 (.out(clock_2_out));
  not not_2 (not_2_out, entrada_2);
  J_K_Flip_Flop j_k_ff_1 (
    .J(entrada_1), .clk(clock_1_out), .K(not_1_out), .Q(j_k_ff_1_q), .reset(clear_1_out));  // open: Qn, preset
  J_K_Flip_Flop j_k_ff_2 (
    .J(entrada_2), .clk(clock_2_out), .K(not_2_out), .Q(j_k_ff_2_q), .reset(clear_2_out));  // open: Qn, preset
  J_K_Flip_Flop j_k_ff_3 (
    .J(j_k_ff_1_q), .clk(clock_1_out), .K(not_3_out), .Q(j_k_ff_3_q), .reset(clear_1_out));  // open: Qn, preset
  not not_3 (not_3_out, j_k_ff_1_q);
  J_K_Flip_Flop j_k_ff_4 (
    .J(j_k_ff_2_q), .clk(clock_2_out), .K(not_4_out), .Q(j_k_ff_4_q), .reset(clear_2_out));  // open: Qn, preset
  not not_4 (not_4_out, j_k_ff_2_q);
  not not_5 (not_5_out, j_k_ff_3_q);
  not not_6 (not_6_out, j_k_ff_4_q);
  J_K_Flip_Flop j_k_ff_5 (
    .J(j_k_ff_3_q), .clk(clock_1_out), .K(not_5_out), .Q(j_k_ff_5_q), .reset(clear_1_out));  // open: Qn, preset
  not not_7 (not_7_out, j_k_ff_5_q);
  J_K_Flip_Flop j_k_ff_6 (
    .J(j_k_ff_4_q), .clk(clock_2_out), .K(not_6_out), .Q(j_k_ff_6_q), .reset(clear_2_out));  // open: Qn, preset
  not not_8 (not_8_out, j_k_ff_6_q);
  J_K_Flip_Flop j_k_ff_7 (
    .J(j_k_ff_5_q), .clk(clock_1_out), .K(not_7_out), .Q(j_k_ff_7_q), .reset(clear_1_out));  // open: Qn, preset
  J_K_Flip_Flop j_k_ff_8 (
    .J(j_k_ff_6_q), .clk(clock_2_out), .K(not_8_out), .Q(j_k_ff_8_q), .reset(clear_2_out));  // open: Qn, preset
  not not_9 (not_9_out, j_k_ff_7_q);
  not not_10 (not_10_out, j_k_ff_8_q);
  J_K_Flip_Flop j_k_ff_9 (
    .J(j_k_ff_7_q), .clk(clock_1_out), .K(not_9_out), .Q(j_k_ff_9_q), .reset(clear_1_out));  // open: Qn, preset
  not not_11 (not_11_out, j_k_ff_9_q);
  J_K_Flip_Flop j_k_ff_10 (
    .J(j_k_ff_8_q), .clk(clock_2_out), .K(not_10_out), .Q(j_k_ff_10_q), .reset(clear_2_out));  // open: Qn, preset
  not not_12 (not_12_out, j_k_ff_10_q);
  J_K_Flip_Flop j_k_ff_11 (
    .J(j_k_ff_9_q), .clk(clock_1_out), .K(not_11_out), .Q(j_k_ff_11_q), .reset(clear_1_out));  // open: Qn, preset
  not not_13 (not_13_out, j_k_ff_11_q);
  J_K_Flip_Flop j_k_ff_12 (
    .J(j_k_ff_10_q), .clk(clock_2_out), .K(not_12_out), .Q(j_k_ff_12_q), .reset(clear_2_out));  // open: Qn, preset
  not not_14 (not_14_out, j_k_ff_12_q);
  J_K_Flip_Flop j_k_ff_13 (
    .J(j_k_ff_11_q), .clk(clock_1_out), .K(not_13_out), .Q(j_k_ff_13_q), .reset(clear_1_out));  // open: Qn, preset
  J_K_Flip_Flop j_k_ff_14 (
    .J(j_k_ff_12_q), .clk(clock_2_out), .K(not_14_out), .Q(j_k_ff_14_q), .reset(clear_2_out));  // open: Qn, preset
  not not_15 (not_15_out, j_k_ff_13_q);
  not not_16 (not_16_out, j_k_ff_14_q);
  J_K_Flip_Flop j_k_ff_15 (
    .J(j_k_ff_13_q), .clk(clock_1_out), .K(not_15_out), .reset(clear_1_out));  // open: Q, Qn, preset
  J_K_Flip_Flop j_k_ff_16 (
    .J(j_k_ff_14_q), .clk(clock_2_out), .K(not_16_out), .reset(clear_2_out));  // open: Q, Qn, preset
endmodule
