// Logisim project G1204.circ as structural Verilog: 1 circuit, main circuit main
module main (
  input  entrada_1,
  input  entrada_2,
  input  entrada_3,
  input  entrada_4
);

  wire clear_1_out, clear_2_out, clear_3_out, clear_4_out, clock__global_out, j_k_ff_1_q, j_k_ff_2_q,
       j_k_ff_3_q, j_k_ff_4_q, j_k_ff_5_q, j_k_ff_6_q, j_k_ff_7_q, j_k_ff_8_q, j_k_ff_9_q, j_k_ff_10_q,
       j_k_ff_11_q, j_k_ff_12_q, j_k_ff_13_q, j_k_ff_14_q, j_k_ff_15_q, j_k_ff_16_q, j_k_ff_17_q,
       j_k_ff_18_q, j_k_ff_19_q, j_k_ff_20_q, j_k_ff_21_q, j_k_ff_22_q, j_k_ff_23_q, j_k_ff_24_q,
       j_k_ff_25_q, j_k_ff_26_q, j_k_ff_27_q, j_k_ff_28_q, not_1_out, not_2_out, not_3_out, not_4_out,
       not_5_out, not_6_out, not_7_out, not_8_out, not_9_out, not_10_out, not_11_out, not_12_out, not_13_out,
       not_14_out, not_15_out, not_16_out, not_17_out, not_18_out, not_19_out, not_20_out, not_21_out,
       not_22_out, not_23_out, not_24_out, not_25_out, not_26_out, not_27_out, not_28_out, not_29_out,
       not_30_out, not_31_out, not_32_out;

  Button clear_1 (.out(clear_1_out));
  Button clear_2 (.out(clear_2_out));
  Button clear_3 (.out(clear_3_out));
  Button clear_4 (.out(clear_4_out));
  Clock clock__global (.out(clock__global_out));
  not not_1 (not_1_out, entrada_1);
  not not_2 (not_2_out, entrada_2);
  not not_3 (not_3_out, entrada_3);
  not not_4 (not_4_out, entrada_4);
  J_K_Flip_Flop j_k_ff_1 (
    .J(entrada_1), .clk(clock__global_out), .K(not_1_out), .Q(j_k_ff_1_q), .reset(clear_1_out));  // open: Qn, preset
  J_K_Flip_Flop j_k_ff_2 (
    .J(entrada_2), .clk(clock__global_out), .K(not_2_out), .Q(j_k_ff_2_q), .reset(clear_2_out));  // open: Qn, preset
  J_K_Flip_Flop j_k_ff_3 (
    .J(entrada_3), .clk(clock__global_out), .K(not_3_out), .Q(j_k_ff_3_q), .reset(clear_3_out));  // open: Qn, preset
  J_K_Flip_Flop j_k_ff_4 (
    .J(entrada_4), .clk(clock__global_out), .K(not_4_out), .Q(j_k_ff_4_q), .reset(clear_4_out));  // open: Qn, preset
  J_K_Flip_Flop j_k_ff_5 (
    .J(j_k_ff_1_q), .clk(clock__global_out), .K(not_5_out), .Q(j_k_ff_5_q), .reset(clear_1_out));  // open: Qn, preset
  not not_5 (not_5_out, j_k_ff_1_q);
  J_K_Flip_Flop j_k_ff_6 (
    .J(j_k_ff_2_q), .clk(clock__global_out), .K(not_6_out), .Q(j_k_ff_6_q), .reset(clear_2_out));  // open: Qn, preset
  not not_6 (not_6_out, j_k_ff_2_q);
  J_K_Flip_Flop j_k_ff_7 (
    .J(j_k_ff_3_q), .clk(clock__global_out), .K(not_7_out), .Q(j_k_ff_7_q), .reset(clear_3_out));  // open: Qn, preset
  not not_7 (not_7_out, j_k_ff_3_q);
  J_K_Flip_Flop j_k_ff_8 (
    .J(j_k_ff_4_q), .clk(clock__global_out), .K(not_8_out), .Q(j_k_ff_8_q), .reset(clear_4_out));  // open: Qn, preset
  not not_8 (not_8_out, j_k_ff_4_q);
  not not_9 (not_9_out, j_k_ff_5_q);
  not not_10 (not_10_out, j_k_ff_6_q);
  not not_11 (not_11_out, j_k_ff_7_q);
  not not_12 (not_12_out, j_k_ff_8_q);
  J_K_Flip_Flop j_k_ff_9 (
    .J(j_k_ff_5_q), .clk(clock__global_out), .K(not_9_out), .Q(j_k_ff_9_q), .reset(clear_1_out));  // open: Qn, preset
  not not_13 (not_13_out, j_k_ff_9_q);
  J_K_Flip_Flop j_k_ff_10 (
    .J(j_k_ff_6_q), .clk(clock__global_out), .K(not_10_out), .Q(j_k_ff_10_q), .reset(clear_2_out));  // open: Qn, preset
  not not_14 (not_14_out, j_k_ff_10_q);
  J_K_Flip_Flop j_k_ff_11 (
    .J(j_k_ff_7_q), .clk(clock__global_out), .K(not_11_out), .Q(j_k_ff_11_q), .reset(clear_3_out));  // open: Qn, preset
  not not_15 (not_15_out, j_k_ff_11_q);
  J_K_Flip_Flop j_k_ff_12 (
    .J(j_k_ff_8_q), .clk(clock__global_out), .K(not_12_out), .Q(j_k_ff_12_q), .reset(clear_4_out));  // open: Qn, preset
  not not_16 (not_16_out, j_k_ff_12_q);
  J_K_Flip_Flop j_k_ff_13 (
    .J(j_k_ff_9_q), .clk(clock__global_out), .K(not_13_out), .Q(j_k_ff_13_q), .reset(clear_1_out));  // open: Qn, preset
  J_K_Flip_Flop j_k_ff_14 (
    .J(j_k_ff_10_q), .clk(clock__global_out), .K(not_14_out), .Q(j_k_ff_14_q), .reset(clear_2_out));  // open: Qn, preset
  J_K_Flip_Flop j_k_ff_15 (
    .J(j_k_ff_11_q), .clk(clock__global_out), .K(not_15_out), .Q(j_k_ff_15_q), .reset(clear_3_out));  // open: Qn, preset
  J_K_Flip_Flop j_k_ff_16 (
    .J(j_k_ff_12_q), .clk(clock__global_out), .K(not_16_out), .Q(j_k_ff_16_q), .reset(clear_4_out));  // open: Qn, preset
  not not_17 (not_17_out, j_k_ff_13_q);
  not not_18 (not_18_out, j_k_ff_14_q);
  not not_19 (not_19_out, j_k_ff_15_q);
  not not_20 (not_20_out, j_k_ff_16_q);
  J_K_Flip_Flop j_k_ff_17 (
    .J(j_k_ff_13_q), .clk(clock__global_out), .K(not_17_out), .Q(j_k_ff_17_q), .reset(clear_1_out));  // open: Qn, preset
  not not_21 (not_21_out, j_k_ff_17_q);
  J_K_Flip_Flop j_k_ff_18 (
    .J(j_k_ff_14_q), .clk(clock__global_out), .K(not_18_out), .Q(j_k_ff_18_q), .reset(clear_2_out));  // open: Qn, preset
  not not_22 (not_22_out, j_k_ff_18_q);
  J_K_Flip_Flop j_k_ff_19 (
    .J(j_k_ff_15_q), .clk(clock__global_out), .K(not_19_out), .Q(j_k_ff_19_q), .reset(clear_3_out));  // open: Qn, preset
  not not_23 (not_23_out, j_k_ff_19_q);
  J_K_Flip_Flop j_k_ff_20 (
    .J(j_k_ff_16_q), .clk(clock__global_out), .K(not_20_out), .Q(j_k_ff_20_q), .reset(clear_4_out));  // open: Qn, preset
  not not_24 (not_24_out, j_k_ff_20_q);
  J_K_Flip_Flop j_k_ff_21 (
    .J(j_k_ff_17_q), .clk(clock__global_out), .K(not_21_out), .Q(j_k_ff_21_q), .reset(clear_1_out));  // open: Qn, preset
  not not_25 (not_25_out, j_k_ff_21_q);
  J_K_Flip_Flop j_k_ff_22 (
    .J(j_k_ff_18_q), .clk(clock__global_out), .K(not_22_out), .Q(j_k_ff_22_q), .reset(clear_2_out));  // open: Qn, preset
  not not_26 (not_26_out, j_k_ff_22_q);
  J_K_Flip_Flop j_k_ff_23 (
    .J(j_k_ff_19_q), .clk(clock__global_out), .K(not_23_out), .Q(j_k_ff_23_q), .reset(clear_3_out));  // open: Qn, preset
  not not_27 (not_27_out, j_k_ff_23_q);
  J_K_Flip_Flop j_k_ff_24 (
    .J(j_k_ff_20_q), .clk(clock__global_out), .K(not_24_out), .Q(j_k_ff_24_q), .reset(clear_4_out));  // open: Qn, preset
  not not_28 (not_28_out, j_k_ff_24_q);
  J_K_Flip_Flop j_k_ff_25 (
    .J(j_k_ff_21_q), .clk(clock__global_out), .K(not_25_out), .Q(j_k_ff_25_q), .reset(clear_1_out));  // open: Qn, preset
  J_K_Flip_Flop j_k_ff_26 (
    .J(j_k_ff_22_q), .clk(clock__global_out), .K(not_26_out), .Q(j_k_ff_26_q), .reset(clear_2_out));  // open: Qn, preset
  J_K_Flip_Flop j_k_ff_27 (
    .J(j_k_ff_23_q), .clk(clock__global_out), .K(not_27_out), .Q(j_k_ff_27_q), .reset(clear_3_out));  // open: Qn, preset
  J_K_Flip_Flop j_k_ff_28 (
    .J(j_k_ff_24_q), .clk(clock__global_out), .K(not_28_out), .Q(j_k_ff_28_q), .reset(clear_4_out));  // open: Qn, preset
  not not_29 (not_29_out, j_k_ff_25_q);
  not not_30 (not_30_out, j_k_ff_26_q);
  not not_31 (not_31_out, j_k_ff_27_q);
  not not_32 (not_32_out, j_k_ff_28_q);
  J_K_Flip_Flop j_k_ff_29 (
    .J(j_k_ff_25_q), .clk(clock__global_out), .K(not_29_out), .reset(clear_1_out));  // open: Q, Qn, preset
  J_K_Flip_Flop j_k_ff_30 (
    .J(j_k_ff_26_q), .clk(clock__global_out), .K(not_30_out), .reset(clear_2_out));  // open: Q, Qn, preset
  J_K_Flip_Flop j_k_ff_31 (
    .J(j_k_ff_27_q), .clk(clock__global_out), .K(not_31_out), .reset(clear_3_out));  // open: Q, Qn, preset
  J_K_Flip_Flop j_k_ff_32 (
    .J(j_k_ff_28_q), .clk(clock__global_out), .K(not_32_out), .reset(clear_4_out));  // open: Q, Qn, preset
endmodule
