// Logisim project G1205.circ as structural Verilog: 1 circuit, main circuit main
module main (
  input  entrada_1,
  input  entrada_2,
  input  entrada_3,
  input  entrada_4,
  input  entrada_5,
  input  entrada_6,
  input  entrada_7,
  input  entrada_8
);

  wire clear_1_out, clear_2_out, clear_3_out, clear_4_out, clear_5_out, clear_6_out, clear_7_out,
       clear_8_out, clock__global_out, j_k_ff_1_q, j_k_ff_2_q, j_k_ff_3_q, j_k_ff_4_q, j_k_ff_5_q,
       j_k_ff_6_q, j_k_ff_7_q, j_k_ff_8_q, j_k_ff_9_q, j_k_ff_10_q, j_k_ff_11_q, j_k_ff_12_q, j_k_ff_13_q,
       j_k_ff_14_q, j_k_ff_15_q, j_k_ff_16_q, j_k_ff_17_q, j_k_ff_18_q, j_k_ff_19_q, j_k_ff_20_q,
       j_k_ff_21_q, j_k_ff_22_q, j_k_ff_23_q, j_k_ff_24_q, j_k_ff_25_q, j_k_ff_26_q, j_k_ff_27_q,
       j_k_ff_28_q, j_k_ff_29_q, j_k_ff_30_q, j_k_ff_31_q, j_k_ff_32_q, j_k_ff_33_q, j_k_ff_34_q,
       j_k_ff_35_q, j_k_ff_36_q, j_k_ff_37_q, j_k_ff_38_q, j_k_ff_39_q, j_k_ff_40_q, j_k_ff_41_q,
       j_k_ff_42_q, j_k_ff_43_q, j_k_ff_44_q, j_k_ff_45_q, j_k_ff_46_q, j_k_ff_47_q, j_k_ff_48_q,
       j_k_ff_49_q, j_k_ff_50_q, j_k_ff_51_q, j_k_ff_52_q, j_k_ff_53_q, j_k_ff_54_q, j_k_ff_55_q,
       j_k_ff_56_q, not_1_out, not_2_out, not_3_out, not_4_out, not_5_out, not_6_out, not_7_out, not_8_out,
       not_9_out, not_10_out, not_11_out, not_12_out, not_13_out, not_14_out, not_15_out, not_16_out,
       not_17_out, not_18_out, not_19_out, not_20_out, not_21_out, not_22_out, not_23_out, not_24_out,
       not_25_out, not_26_out, not_27_out, not_28_out, not_29_out, not_30_out, not_31_out, not_32_out,
       not_33_out, not_34_out, not_35_out, not_36_out, not_37_out, not_38_out, not_39_out, not_40_out,
       not_41_out, not_42_out, not_43_out, not_44_out, not_45_out, not_46_out, not_47_out, not_48_out,
       not_49_out, not_50_out, not_51_out, not_52_out, not_53_out, not_54_out, not_55_out, not_56_out,
       not_57_out, not_58_out, not_59_out, not_60_out, not_61_out, not_62_out, not_63_out, not_64_out;

  Button clear_1 (.out(clear_1_out));
  Button clear_2 (.out(clear_2_out));
  Button clear_3 (.out(clear_3_out));
  Button clear_4 (.out(clear_4_out));
  Button clear_5 (.out(clear_5_out));
  Button clear_6 (.out(clear_6_out));
  Button clear_7 (.out(clear_7_out));
  Button clear_8 (.out(clear_8_out));
  Clock clock__global (.out(clock__global_out));
  not not_1 (not_1_out, entrada_1);
  not not_2 (not_2_out, entrada_2);
  not not_3 (not_3_out, entrada_3);
  not not_4 (not_4_out, entrada_4);
  not not_5 (not_5_out, entrada_5);
  not not_6 (not_6_out, entrada_6);
  not not_7 (not_7_out, entrada_7);
  not not_8 (not_8_out, entrada_8);
  J_K_Flip_Flop j_k_ff_1 (
    .J(entrada_1), .clk(clock__global_out), .K(not_1_out), .Q(j_k_ff_1_q), .reset(clear_1_out));  // open: Qn, preset
  J_K_Flip_Flop j_k_ff_2 (
    .J(entrada_2), .clk(clock__global_out), .K(not_2_out), .Q(j_k_ff_2_q), .reset(clear_2_out));  // open: Qn, preset
  J_K_Flip_Flop j_k_ff_3 (
    .J(entrada_3), .clk(clock__global_out), .K(not_3_out), .Q(j_k_ff_3_q), .reset(clear_3_out));  // open: Qn, preset
  J_K_Flip_Flop j_k_ff_4 (
    .J(entrada_4), .clk(clock__global_out), .K(not_4_out), .Q(j_k_ff_4_q), .reset(clear_4_out));  // open: Qn, preset
  J_K_Flip_Flop j_k_ff_5 (
    .J(entrada_5), .clk(clock__global_out), .K(not_5_out), .Q(j_k_ff_5_q), .reset(clear_5_out));  // open: Qn, preset
  J_K_Flip_Flop j_k_ff_6 (
    .J(entrada_6), .clk(clock__global_out), .K(not_6_out), .Q(j_k_ff_6_q), .reset(clear_6_out));  // open: Qn, preset
  J_K_Flip_Flop j_k_ff_7 (
    .J(entrada_7), .clk(clock__global_out), .K(not_7_out), .Q(j_k_ff_7_q), .reset(clear_7_out));  // open: Qn, preset
  J_K_Flip_Flop j_k_ff_8 (
    .J(entrada_8), .clk(clock__global_out), .K(not_8_out), .Q(j_k_ff_8_q), .reset(clear_8_out));  // open: Qn, preset
  J_K_Flip_Flop j_k_ff_9 (
    .J(j_k_ff_1_q), .clk(clock__global_out), .K(not_9_out), .Q(j_k_ff_9_q), .reset(clear_1_out));  // open: Qn, preset
  not not_9 (not_9_out, j_k_ff_1_q);
  J_K_Flip_Flop j_k_ff_10 (
    .J(j_k_ff_2_q), .clk(clock__global_out), .K(not_10_out), .Q(j_k_ff_10_q), .reset(clear_2_out));  // open: Qn, preset
  not not_10 (not_10_out, j_k_ff_2_q);
  J_K_Flip_Flop j_k_ff_11 (
    .J(j_k_ff_3_q), .clk(clock__global_out), .K(not_11_out), .Q(j_k_ff_11_q), .reset(clear_3_out));  // open: Qn, preset
  not not_11 (not_11_out, j_k_ff_3_q);
  J_K_Flip_Flop j_k_ff_12 (
    .J(j_k_ff_4_q), .clk(clock__global_out), .K(not_12_out), .Q(j_k_ff_12_q), .reset(clear_4_out));  // open: Qn, preset
  not not_12 (not_12_out, j_k_ff_4_q);
  J_K_Flip_Flop j_k_ff_13 (
    .J(j_k_ff_5_q), .clk(clock__global_out), .K(not_13_out), .Q(j_k_ff_13_q), .reset(clear_5_out));  // open: Qn, preset
  not not_13 (not_13_out, j_k_ff_5_q);
  J_K_Flip_Flop j_k_ff_14 (
    .J(j_k_ff_6_q), .clk(clock__global_out), .K(not_14_out), .Q(j_k_ff_14_q), .reset(clear_6_out));  // open: Qn, preset
  not not_14 (not_14_out, j_k_ff_6_q);
  J_K_Flip_Flop j_k_ff_15 (
    .J(j_k_ff_7_q), .clk(clock__global_out), .K(not_15_out), .Q(j_k_ff_15_q), .reset(clear_7_out));  // open: Qn, preset
  not not_15 (not_15_out, j_k_ff_7_q);
  J_K_Flip_Flop j_k_ff_16 (
    .J(j_k_ff_8_q), .clk(clock__global_out), .K(not_16_out), .Q(j_k_ff_16_q), .reset(clear_8_out));  // open: Qn, preset
  not not_16 (not_16_out, j_k_ff_8_q);
  not not_17 (not_17_out, j_k_ff_9_q);
  not not_18 (not_18_out, j_k_ff_10_q);
  not not_19 (not_19_out, j_k_ff_11_q);
  not not_20 (not_20_out, j_k_ff_12_q);
  not not_21 (not_21_out, j_k_ff_13_q);
  not not_22 (not_22_out, j_k_ff_14_q);
  not not_23 (not_23_out, j_k_ff_15_q);
  not not_24 (not_24_out, j_k_ff_16_q);
  J_K_Flip_Flop j_k_ff_17 (
    .J(j_k_ff_9_q), .clk(clock__global_out), .K(not_17_out), .Q(j_k_ff_17_q), .reset(clear_1_out));  // open: Qn, preset
  not not_25 (not_25_out, j_k_ff_17_q);
  J_K_Flip_Flop j_k_ff_18 (
    .J(j_k_ff_10_q), .clk(clock__global_out), .K(not_18_out), .Q(j_k_ff_18_q), .reset(clear_2_out));  // open: Qn, preset
  not not_26 (not_26_out, j_k_ff_18_q);
  J_K_Flip_Flop j_k_ff_19 (
    .J(j_k_ff_11_q), .clk(clock__global_out), .K(not_19_out), .Q(j_k_ff_19_q), .reset(clear_3_out));  // open: Qn, preset
  not not_27 (not_27_out, j_k_ff_19_q);
  J_K_Flip_Flop j_k_ff_20 (
    .J(j_k_ff_12_q), .clk(clock__global_out), .K(not_20_out), .Q(j_k_ff_20_q), .reset(clear_4_out));  // open: Qn, preset
  not not_28 (not_28_out, j_k_ff_20_q);
  J_K_Flip_Flop j_k_ff_21 (
    .J(j_k_ff_13_q), .clk(clock__global_out), .K(not_21_out), .Q(j_k_ff_21_q), .reset(clear_5_out));  // open: Qn, preset
  not not_29 (not_29_out, j_k_ff_21_q);
  J_K_Flip_Flop j_k_ff_22 (
    .J(j_k_ff_14_q), .clk(clock__global_out), .K(not_22_out), .Q(j_k_ff_22_q), .reset(clear_6_out));  // open: Qn, preset
  not not_30 (not_30_out, j_k_ff_22_q);
  J_K_Flip_Flop j_k_ff_23 (
    .J(j_k_ff_15_q), .clk(clock__global_out), .K(not_23_out), .Q(j_k_ff_23_q), .reset(clear_7_out));  // open: Qn, preset
  not not_31 (not_31_out, j_k_ff_23_q);
  J_K_Flip_Flop j_k_ff_24 (
    .J(j_k_ff_16_q), .clk(clock__global_out), .K(not_24_out), .Q(j_k_ff_24_q), .reset(clear_8_out));  // open: Qn, preset
  not not_32 (not_32_out, j_k_ff_24_q);
  J_K_Flip_Flop j_k_ff_25 (
    .J(j_k_ff_17_q), .clk(clock__global_out), .K(not_25_out), .Q(j_k_ff_25_q), .reset(clear_1_out));  // open: Qn, preset
  J_K_Flip_Flop j_k_ff_26 (
    .J(j_k_ff_18_q), .clk(clock__global_out), .K(not_26_out), .Q(j_k_ff_26_q), .reset(clear_2_out));  // open: Qn, preset
  J_K_Flip_Flop j_k_ff_27 (
    .J(j_k_ff_19_q), .clk(clock__global_out), .K(not_27_out), .Q(j_k_ff_27_q), .reset(clear_3_out));  // open: Qn, preset
  J_K_Flip_Flop j_k_ff_28 (
    .J(j_k_ff_20_q), .clk(clock__global_out), .K(not_28_out), .Q(j_k_ff_28_q), .reset(clear_4_out));  // open: Qn, preset
  J_K_Flip_Flop j_k_ff_29 (
    .J(j_k_ff_21_q), .clk(clock__global_out), .K(not_29_out), .Q(j_k_ff_29_q), .reset(clear_5_out));  // open: Qn, preset
  J_K_Flip_Flop j_k_ff_30 (
    .J(j_k_ff_22_q), .clk(clock__global_out), .K(not_30_out), .Q(j_k_ff_30_q), .reset(clear_6_out));  // open: Qn, preset
  J_K_Flip_Flop j_k_ff_31 (
    .J(j_k_ff_23_q), .clk(clock__global_out), .K(not_31_out), .Q(j_k_ff_31_q), .reset(clear_7_out));  // open: Qn, preset
  J_K_Flip_Flop j_k_ff_32 (
    .J(j_k_ff_24_q), .clk(clock__global_out), .K(not_32_out), .Q(j_k_ff_32_q), .reset(clear_8_out));  // open: Qn, preset
  not not_33 (not_33_out, j_k_ff_25_q);
  not not_34 (not_34_out, j_k_ff_26_q);
  not not_35 (not_35_out, j_k_ff_27_q);
  not not_36 (not_36_out, j_k_ff_28_q);
  not not_37 (not_37_out, j_k_ff_29_q);
  not not_38 (not_38_out, j_k_ff_30_q);
  not not_39 (not_39_out, j_k_ff_31_q);
  not not_40 (not_40_out, j_k_ff_32_q);
  J_K_Flip_Flop j_k_ff_33 (
    .J(j_k_ff_25_q), .clk(clock__global_out), .K(not_33_out), .Q(j_k_ff_33_q), .reset(clear_1_out));  // open: Qn, preset
  not not_41 (not_41_out, j_k_ff_33_q);
  J_K_Flip_Flop j_k_ff_34 (
    .J(j_k_ff_26_q), .clk(clock__global_out), .K(not_34_out), .Q(j_k_ff_34_q), .reset(clear_2_out));  // open: Qn, preset
  not not_42 (not_42_out, j_k_ff_34_q);
  J_K_Flip_Flop j_k_ff_35 (
    .J(j_k_ff_27_q), .clk(clock__global_out), .K(not_35_out), .Q(j_k_ff_35_q), .reset(clear_3_out));  // open: Qn, preset
  not not_43 (not_43_out, j_k_ff_35_q);
  J_K_Flip_Flop j_k_ff_36 (
    .J(j_k_ff_28_q), .clk(clock__global_out), .K(not_36_out), .Q(j_k_ff_36_q), .reset(clear_4_out));  // open: Qn, preset
  not not_44 (not_44_out, j_k_ff_36_q);
  J_K_Flip_Flop j_k_ff_37 (
    .J(j_k_ff_29_q), .clk(clock__global_out), .K(not_37_out), .Q(j_k_ff_37_q), .reset(clear_5_out));  // open: Qn, preset
  not not_45 (not_45_out, j_k_ff_37_q);
  J_K_Flip_Flop j_k_ff_38 (
    .J(j_k_ff_30_q), .clk(clock__global_out), .K(not_38_out), .Q(j_k_ff_38_q), .reset(clear_6_out));  // open: Qn, preset
  not not_46 (not_46_out, j_k_ff_38_q);
  J_K_Flip_Flop j_k_ff_39 (
    .J(j_k_ff_31_q), .clk(clock__global_out), .K(not_39_out), .Q(j_k_ff_39_q), .reset(clear_7_out));  // open: Qn, preset
  not not_47 (not_47_out, j_k_ff_39_q);
  J_K_Flip_Flop j_k_ff_40 (
    .J(j_k_ff_32_q), .clk(clock__global_out), .K(not_40_out), .Q(j_k_ff_40_q), .reset(clear_8_out));  // open: Qn, preset
  not not_48 (not_48_out, j_k_ff_40_q);
  J_K_Flip_Flop j_k_ff_41 (
    .J(j_k_ff_33_q), .clk(clock__global_out), .K(not_41_out), .Q(j_k_ff_41_q), .reset(clear_1_out));  // open: Qn, preset
  not not_49 (not_49_out, j_k_ff_41_q);
  J_K_Flip_Flop j_k_ff_42 (
    .J(j_k_ff_34_q), .clk(clock__global_out), .K(not_42_out), .Q(j_k_ff_42_q), .reset(clear_2_out));  // open: Qn, preset
  not not_50 (not_50_out, j_k_ff_42_q);
  J_K_Flip_Flop j_k_ff_43 (
    .J(j_k_ff_35_q), .clk(clock__global_out), .K(not_43_out), .Q(j_k_ff_43_q), .reset(clear_3_out));  // open: Qn, preset
  not not_51 (not_51_out, j_k_ff_43_q);
  J_K_Flip_Flop j_k_ff_44 (
    .J(j_k_ff_36_q), .clk(clock__global_out), .K(not_44_out), .Q(j_k_ff_44_q), .reset(clear_4_out));  // open: Qn, preset
  not not_52 (not_52_out, j_k_ff_44_q);
  J_K_Flip_Flop j_k_ff_45 (
    .J(j_k_ff_37_q), .clk(clock__global_out), .K(not_45_out), .Q(j_k_ff_45_q), .reset(clear_5_out));  // open: Qn, preset
  not not_53 (not_53_out, j_k_ff_45_q);
  J_K_Flip_Flop j_k_ff_46 (
    .J(j_k_ff_38_q), .clk(clock__global_out), .K(not_46_out), .Q(j_k_ff_46_q), .reset(clear_6_out));  // open: Qn, preset
  not not_54 (not_54_out, j_k_ff_46_q);
  J_K_Flip_Flop j_k_ff_47 (
    .J(j_k_ff_39_q), .clk(clock__global_out), .K(not_47_out), .Q(j_k_ff_47_q), .reset(clear_7_out));  // open: Qn, preset
  not not_55 (not_55_out, j_k_ff_47_q);
  J_K_Flip_Flop j_k_ff_48 (
    .J(j_k_ff_40_q), .clk(clock__global_out), .K(not_48_out), .Q(j_k_ff_48_q), .reset(clear_8_out));  // open: Qn, preset
  not not_56 (not_56_out, j_k_ff_48_q);
  J_K_Flip_Flop j_k_ff_49 (
    .J(j_k_ff_41_q), .clk(clock__global_out), .K(not_49_out), .Q(j_k_ff_49_q), .reset(clear_1_out));  // open: Qn, preset
  J_K_Flip_Flop j_k_ff_50 (
    .J(j_k_ff_42_q), .clk(clock__global_out), .K(not_50_out), .Q(j_k_ff_50_q), .reset(clear_2_out));  // open: Qn, preset
  J_K_Flip_Flop j_k_ff_51 (
    .J(j_k_ff_43_q), .clk(clock__global_out), .K(not_51_out), .Q(j_k_ff_51_q), .reset(clear_3_out));  // open: Qn, preset
  J_K_Flip_Flop j_k_ff_52 (
    .J(j_k_ff_44_q), .clk(clock__global_out), .K(not_52_out), .Q(j_k_ff_52_q), .reset(clear_4_out));  // open: Qn, preset
  J_K_Flip_Flop j_k_ff_53 (
    .J(j_k_ff_45_q), .clk(clock__global_out), .K(not_53_out), .Q(j_k_ff_53_q), .reset(clear_5_out));  // open: Qn, preset
  J_K_Flip_Flop j_k_ff_54 (
    .J(j_k_ff_46_q), .clk(clock__global_out), .K(not_54_out), .Q(j_k_ff_54_q), .reset(clear_6_out));  // open: Qn, preset
  J_K_Flip_Flop j_k_ff_55 (
    .J(j_k_ff_47_q), .clk(clock__global_out), .K(not_55_out), .Q(j_k_ff_55_q), .reset(clear_7_out));  // open: Qn, preset
  J_K_Flip_Flop j_k_ff_56 (
    .J(j_k_ff_48_q), .clk(clock__global_out), .K(not_56_out), .Q(j_k_ff_56_q), .reset(clear_8_out));  // open: Qn, preset
  not not_57 (not_57_out, j_k_ff_49_q);
  not not_58 (not_58_out, j_k_ff_50_q);
  not not_59 (not_59_out, j_k_ff_51_q);
  not not_60 (not_60_out, j_k_ff_52_q);
  not not_61 (not_61_out, j_k_ff_53_q);
  not not_62 (not_62_out, j_k_ff_54_q);
  not not_63 (not_63_out, j_k_ff_55_q);
  not not_64 (not_64_out, j_k_ff_56_q);
  J_K_Flip_Flop j_k_ff_57 (
    .J(j_k_ff_49_q), .clk(clock__global_out), .K(not_57_out), .reset(clear_1_out));  // open: Q, Qn, preset
  J_K_Flip_Flop j_k_ff_58 (
    .J(j_k_ff_50_q), .clk(clock__global_out), .K(not_58_out), .reset(clear_2_out));  // open: Q, Qn, preset
  J_K_Flip_Flop j_k_ff_59 (
    .J(j_k_ff_51_q), .clk(clock__global_out), .K(not_59_out), .reset(clear_3_out));  // open: Q, Qn, preset
  J_K_Flip_Flop j_k_ff_60 (
    .J(j_k_ff_52_q), .clk(clock__global_out), .K(not_60_out), .reset(clear_4_out));  // open: Q, Qn, preset
  J_K_Flip_Flop j_k_ff_61 (
    .J(j_k_ff_53_q), .clk(clock__global_out), .K(not_61_out), .reset(clear_5_out));  // open: Q, Qn, preset
  J_K_Flip_Flop j_k_ff_62 (
    .J(j_k_ff_54_q), .clk(clock__global_out), .K(not_62_out), .reset(clear_6_out));  // open: Q, Qn, preset
  J_K_Flip_Flop j_k_ff_63 (
    .J(j_k_ff_55_q), .clk(clock__global_out), .K(not_63_out), .reset(clear_7_out));  // open: Q, Qn, preset
  J_K_Flip_Flop j_k_ff_64 (
    .J(j_k_ff_56_q), .clk(clock__global_out), .K(not_64_out), .reset(clear_8_out));  // open: Q, Qn, preset
endmodule
