// Logisim project G1301.circ as structural Verilog: 1 circuit, main circuit main
module main (
  output out_1,
  output out_2,
  output out_3,
  output out_4,
  output out_5,
  output out_6
);

  wire Clock_out, Reset__1_out;

  Button Reset__1 (.out(Reset__1_out));
  Clock Clock (.out(Clock_out));
  J_K_Flip_Flop _2_5 (.J(1'b1), .clk(out_2), .K(1'b1), .Q(out_1), .preset(Reset__1_out));  // open: Qn, reset
  J_K_Flip_Flop _2_4 (.J(1'b1), .clk(out_3), .K(1'b1), .Q(out_2), .preset(Reset__1_out));  // open: Qn, reset
  J_K_Flip_Flop _2_3 (.J(1'b1), .clk(out_4), .K(1'b1), .Q(out_3), .preset(Reset__1_out));  // open: Qn, reset
  J_K_Flip_Flop _2_2 (.J(1'b1), .clk(out_5), .K(1'b1), .Q(out_4), .preset(Reset__1_out));  // open: Qn, reset
  J_K_Flip_Flop _2_1 (.J(1'b1), .clk(out_6), .K(1'b1), .Q(out_5), .preset(Reset__1_out));  // open: Qn, reset
  J_K_Flip_Flop _2_0 (.J(1'b1), .clk(Clock_out), .K(1'b1), .Q(out_6), .preset(Reset__1_out));  // open: Qn, reset
endmodule
