// Logisim project G1304.circ as structural Verilog: 1 circuit, main circuit main
module main (
  output out_1,
  output out_2,
  output out_3,
  output out_4,
  output out_5
);

  wire and_1_out, Clock_out, not_1_out, not_2_out, not_3_out, or_1_out, Reset__1_out;

  Button Reset__1 (.out(Reset__1_out));
  or or_1 (or_1_out, Reset__1_out, and_1_out);
  Clock Clock (.out(Clock_out));
  J_K_Flip_Flop _2_4 (.J(1'b1), .clk(out_2), .K(1'b1), .Q(out_1), .preset(or_1_out));  // open: Qn, reset
  J_K_Flip_Flop _2_3 (.J(1'b1), .clk(out_3), .K(1'b1), .Q(out_2), .preset(or_1_out));  // open: Qn, reset
  J_K_Flip_Flop _2_2 (.J(1'b1), .clk(out_4), .K(1'b1), .Q(out_3), .preset(or_1_out));  // open: Qn, reset
  not not_1 (not_1_out, out_5);
  not not_2 (not_2_out, out_3);
  and and_1 (and_1_out, not_1_out, out_4, not_2_out, out_2, not_3_out);
  not not_3 (not_3_out, out_1);
  J_K_Flip_Flop _2_1 (.J(1'b1), .clk(out_5), .K(1'b1), .Q(out_4), .preset(or_1_out));  // open: Qn, reset
  J_K_Flip_Flop _2_0 (.J(1'b1), .clk(Clock_out), .K(1'b1), .Q(out_5), .preset(or_1_out));  // open: Qn, reset
endmodule
