// Logisim project G1305.circ as structural Verilog: 1 circuit, main circuit main
module main (
  output out_1,
  output out_2,
  output out_3
);

  wire and_1_out, and_2_out, button_1_out, clock_1_out, or_1_out;

  Clock clock_1 (.out(clock_1_out));
  Button button_1 (.out(button_1_out));
  or or_1 (or_1_out, button_1_out, and_1_out);
  and and_1 (and_1_out, out_3, out_2, out_1);
  T_Flip_Flop t_ff_1 (.clk(clock_1_out), .T(1'b1), .Q(out_1), .reset(or_1_out));  // open: Qn, preset
  T_Flip_Flop t_ff_2 (.clk(clock_1_out), .T(out_1), .Q(out_2), .reset(or_1_out));  // open: Qn, preset
  and and_2 (and_2_out, out_1, out_2);
  T_Flip_Flop t_ff_3 (.clk(clock_1_out), .T(and_2_out), .Q(out_3), .reset(or_1_out));  // open: Qn, preset
endmodule
