// Logisim project G1306.circ as structural Verilog: 1 circuit, main circuit main
module main (
  output out_1,
  output out_2,
  output out_3,
  output out_4,
  output out_5,
  output out_6
);

  wire and_1_out, and_2_out, and_3_out, and_4_out, and_5_out, and_6_out, clock_1_out, not_1_out, or_1_out,
       Reset_out;

  Clock clock_1 (.out(clock_1_out));
  not not_1 (not_1_out, or_1_out);
  Button Reset (.out(Reset_out));
  or or_1 (or_1_out, out_2, out_3, out_4, out_5);
  and and_1 (and_1_out, not_1_out, 1'b1);
  J_K_Flip_Flop j_k_ff_1 (
    .J(and_1_out), .clk(clock_1_out), .K(1'b1), .Q(out_1), .reset(Reset_out));  // open: Qn, preset
  and and_2 (and_2_out, out_1, 1'b1);
  J_K_Flip_Flop j_k_ff_2 (
    .J(and_2_out), .clk(clock_1_out), .K(1'b1), .Q(out_2), .reset(Reset_out));  // open: Qn, preset
  and and_3 (and_3_out, out_2, 1'b1);
  J_K_Flip_Flop j_k_ff_3 (
    .J(and_3_out), .clk(clock_1_out), .K(1'b1), .Q(out_3), .reset(Reset_out));  // open: Qn, preset
  and and_4 (and_4_out, out_3, 1'b1);
  J_K_Flip_Flop j_k_ff_4 (
    .J(and_4_out), .clk(clock_1_out), .K(1'b1), .Q(out_4), .reset(Reset_out));  // open: Qn, preset
  and and_5 (and_5_out, out_4, 1'b1);
  J_K_Flip_Flop j_k_ff_5 (
    .J(and_5_out), .clk(clock_1_out), .K(1'b1), .Q(out_5), .reset(Reset_out));  // open: Qn, preset
  and and_6 (and_6_out, out_5, 1'b1);
  J_K_Flip_Flop j_k_ff_6 (
    .J(and_6_out), .clk(clock_1_out), .K(1'b1), .Q(out_6), .reset(Reset_out));  // open: Qn, preset
endmodule
