// Logisim project G1401.circ as structural Verilog: 1 circuit, main circuit main
module main (
  input  Entrada_do_primeiro_pino,
  output out_2,
  output out_3,
  output out_4,
  output out_5,
  output out_6
);

  wire Clear_out, Clock_out;

  Clock Clock (.out(Clock_out));
  Button Clear (.out(Clear_out));
  D_Flip_Flop d_ff_1 (.clk(Clock_out), .D(out_3), .Q(out_2), .reset(Clear_out));  // open: Qn, preset
  D_Flip_Flop d_ff_2 (.clk(Clock_out), .D(out_4), .Q(out_3), .reset(Clear_out));  // open: Qn, preset
  D_Flip_Flop d_ff_3 (.clk(Clock_out), .D(out_5), .Q(out_4), .reset(Clear_out));  // open: Qn, preset
  D_Flip_Flop d_ff_4 (.clk(Clock_out), .D(out_6), .Q(out_5), .reset(Clear_out));  // open: Qn, preset
  D_Flip_Flop d_ff_5 (.clk(Clock_out), .D(Entrada_do_primeiro_pino), .Q(out_6), .reset(Clear_out));  // open: Qn, preset
endmodule
