// Logisim project G1405.circ as structural Verilog: 1 circuit, main circuit main
module main (
  input  in_1,
  input  entrada_1,
  input  entrada_2,
  input  entrada_3,
  input  entrada_4,
  input  entrada_5,
  output saida_serial
);

  wire and_1_out, and_2_out, and_3_out, and_4_out, and_5_out, clock_out, d_ff_1_q, d_ff_2_q, d_ff_3_q,
       d_ff_4_q, LD_out, reset_out;

  Button clock (.out(clock_out));
  Button reset (.out(reset_out));
  Button LD (.out(LD_out));
  and and_1 (and_1_out, entrada_1, LD_out);
  D_Flip_Flop d_ff_1 (.clk(clock_out), .D(in_1), .Q(d_ff_1_q), .preset(and_1_out), .reset(reset_out));  // open: Qn
  D_Flip_Flop d_ff_2 (.clk(clock_out), .D(d_ff_1_q), .Q(d_ff_2_q), .preset(and_2_out), .reset(reset_out));  // open: Qn
  and and_2 (and_2_out, entrada_2, LD_out);
  D_Flip_Flop d_ff_3 (.clk(clock_out), .D(d_ff_2_q), .Q(d_ff_3_q), .preset(and_3_out), .reset(reset_out));  // open: Qn
  and and_3 (and_3_out, entrada_3, LD_out);
  and and_4 (and_4_out, entrada_4, LD_out);
  D_Flip_Flop d_ff_4 (.clk(clock_out), .D(d_ff_3_q), .Q(d_ff_4_q), .preset(and_4_out), .reset(reset_out));  // open: Qn
  D_Flip_Flop d_ff_5 (
    .clk(clock_out), .D(d_ff_4_q), .Q(saida_serial), .preset(and_5_out), .reset(reset_out));  // open: Qn
  and and_5 (and_5_out, entrada_5, LD_out);
endmodule
