// Logisim project Q03.circ as structural Verilog: 1 circuit, main circuit main
module main (
  input  A,
  input  B,
  input  C,
  output out_4
);

  wire not_1_out, or_1_out, or_2_out, or_3_out;

  or or_1 (or_1_out, C, not_1_out);
  not not_1 (not_1_out, A);
  or or_2 (or_2_out, B, A);
  or or_3 (or_3_out, C, B);
  and and_1 (out_4, or_1_out, or_2_out, or_3_out);

  // Notes on the sheet:
  //   Questão 3
endmodule
