// Logisim project Q03.circ as structural Verilog: 1 circuit, main circuit main
module main (
  output Q1,
  output Q2,
  output Q3
);

  wire clock_1_out;

  Clock clock_1 (.out(clock_1_out));
  J_K_Flip_Flop j_k_ff_1 (.J(1'b1), .clk(clock_1_out), .K(1'b1), .Q(Q1));  // open: Qn, preset, reset
  J_K_Flip_Flop j_k_ff_2 (.J(1'b1), .clk(Q1), .K(1'b1), .Q(Q2));  // open: Qn, preset, reset
  J_K_Flip_Flop j_k_ff_3 (.J(1'b1), .clk(Q2), .K(1'b1), .Q(Q3));  // open: Qn, preset, reset
endmodule
